// Digital circuit 01.dig as structural Verilog
module _01 (
  input  X1,
  input  X2,
  input  X3,
  input  X4,
  output Y1,
  output [4:0] CheckGlitch
);

  wire and_1_out, and_2_out;

  and and_1 (and_1_out, X2, X3, X4);
  and and_2 (and_2_out, X1, ~X3);  // And
  or or_1 (Y1, and_1_out, and_2_out);
  Counter #(.Bits(5)) counter_1 (.en(1'b1), .C(Y1), .clr(1'b0), .out(CheckGlitch));  // open: ovf

  // Other names for the same wires on the sheet: A = X1; B = X2; C = X3; D = X4

  // Notes on the sheet:
  //   Must not change this section
endmodule
