// Digital circuit 02.dig as structural Verilog
module _02 (
  input  X1,
  input  X0,
  input  Y1,
  input  Y0,
  output [4:0] Z
);

  wire [4:0] x2, x3;
  wire [9:5] mul_1_mul, mul_2_mul;

  Multiplexer #(.Bits(5), .Selector_Bits(2)) multiplexer_1 (
    .sel({Y1, Y0}), .in_0(5'b00001), .in_1({3'b000, X1, X0}), .in_2(x2), .in_3(x3), .out(Z));
  Mul #(.Bits(5)) mul_1 (.a({3'b000, X1, X0}), .b({3'b000, X1, X0}), .mul({mul_1_mul, x2}));
  Mul #(.Bits(5)) mul_2 (.a({3'b000, X1, X0}), .b(x2), .mul({mul_2_mul, x3}));
endmodule
