// Digital circuit 01_passed.dig as structural Verilog
module _01_passed (
  input  reset,
  input  clk,
  output A,
  output B,
  output C
);

  wire [2:0] multiplexer_1_out, multiplexer_2_out;

  Multiplexer #(.Bits(3), .Selector_Bits(3)) multiplexer_1 (
    .sel({A, B, C}), .in_0(3'b001), .in_1(3'b011), .in_2(3'b110), .in_3(3'b010), .in_4(3'b000),
    .in_5(3'b100), .in_6(3'b111), .in_7(3'b101), .out(multiplexer_1_out));
  Multiplexer #(.Bits(3)) multiplexer_2 (.sel(reset), .in_0(multiplexer_1_out), .in_1(3'b000), .out(multiplexer_2_out));
  D_FF #(.Bits(3)) d_ff_1 (.D(multiplexer_2_out), .C(clk), .Q({A, B, C}));  // open: nQ

  // Other names for the same wires on the sheet: current[2:0] = {A, B, C}
endmodule
