// Digital circuit 03.dig as structural Verilog
module _03 (
  input  [15:0] A,
  input  \input ,
  input  clk,
  input  reset,
  output busy,
  output [15:0] mean
);

  wire and_1_out, d_ff_1_q, mean_t, multiplexer_1_out, run;

  Multiplexer multiplexer_1 (.sel(reset), .in_0(\input ), .in_1(1'b0), .out(multiplexer_1_out));
  D_FF d_ff_1 (.D(multiplexer_1_out), .C(clk), .Q(d_ff_1_q));  // open: nQ
  and and_1 (and_1_out, ~d_ff_1_q, \input );  // And
  and and_2 (run, ~busy, and_1_out);  // And
  Multiplexer multiplexer_2 (.sel(reset), .in_1(1'b0), .out(mean_t));  // open: in_0
  D_FF d_ff_2 (.D(run), .C(clk), .Q(busy));  // open: nQ
  // Pins of 1 and 16 bits meet at {16{1'b0}}
endmodule
