// Digital circuit 02.dig as structural Verilog
module _02 (
  input  reset,
  input  [15:0] P,
  input  start,
  input  clock,
  output [15:0] W,
  output [15:0] H,
  output [31:0] A,
  output busy
);

  wire and_1_out, d_ff_1_q, multiplexer_1_out, run;
  wire [15:0] div_1_q, div_2_q, multiplexer_2_out, multiplexer_3_out, sub_1_s;

  Multiplexer multiplexer_1 (.sel(reset), .in_0(start), .in_1(1'b0), .out(multiplexer_1_out));
  Div #(.Bits(16)) div_1 (.a(P), .b(16'h2), .q(div_1_q));  // open: r
  D_FF d_ff_1 (.D(multiplexer_1_out), .C(clock), .Q(d_ff_1_q));  // open: nQ
  and and_1 (and_1_out, ~d_ff_1_q, start);  // And
  Div #(.Bits(16)) div_2 (.a(div_1_q), .b(16'h2), .q(div_2_q));  // open: r
  Sub #(.Bits(16)) sub_1 (.a(div_1_q), .b(div_2_q), .c_i(1'b0), .s(sub_1_s));  // open: c_o
  Multiplexer #(.Bits(16)) multiplexer_2 (.sel(run), .in_0(H), .in_1(div_2_q), .out(multiplexer_2_out));
  Multiplexer #(.Bits(16)) multiplexer_3 (.sel(run), .in_0(W), .in_1(sub_1_s), .out(multiplexer_3_out));
  and and_2 (run, ~busy, and_1_out);  // And
  D_FF #(.Bits(16)) d_ff_2 (.D(multiplexer_2_out), .C(clock), .Q(H));  // open: nQ
  D_FF #(.Bits(16)) d_ff_3 (.D(multiplexer_3_out), .C(clock), .Q(W));  // open: nQ
  D_FF d_ff_4 (.D(run), .C(clock), .Q(busy));  // open: nQ
  Mul #(.Bits(16)) mul_1 (.a(H), .b(W), .mul(A));

  // Other names for the same wires on the sheet: clk = clock
endmodule

/* Test case T01:
P start clock reset W H A busy
0 0 0 1 x x x x
0 0 1 1 x x x x
0 0 0 0 0 0 0 0
0 0 1 0 0 0 0 0
92 1 0 0 x x x x
92 1 1 0 x x x x
0 0 0 0 x x x x
0 0 1 0 x x x x
0 0 0 0 x x x x
0 0 1 0 x x x x
0 0 0 0 x x x x
0 0 1 0 x x x x
0 0 0 0 x x x x
0 0 1 0 x x x x
0 0 0 0 x x x x
0 0 1 0 x x x x
0 0 0 0 x x x x
0 0 1 0 x x x x
0 0 0 0 x x x x
0 0 1 0 x x x x
0 0 0 0 x x x x
0 0 1 0 x x x x
0 0 0 0 x x x x
0 0 1 0 x x x x
0 0 0 0 x x x x
0 0 1 0 x x x x
0 0 0 0 x x x x
0 0 1 0 x x x x
0 0 0 0 x x x x
0 0 1 0 x x x x
0 0 0 0 x x x x
0 0 1 0 x x x x
0 0 0 0 x x x x
0 0 1 0 x x x x
0 0 0 0 x x x x
0 0 1 0 x x x x
0 0 0 0 x x x x
0 0 1 0 x x x x
0 0 0 0 x x x x
0 0 1 0 x x x x
0 0 0 0 x x x x
0 0 1 0 x x x x
0 0 0 0 x x x x
0 0 1 0 x x x x
0 0 0 0 x x x x
0 0 1 0 x x x x
0 0 0 0 x x x x
0 0 1 0 x x x x
0 0 0 0 x x x x
0 0 1 0 x x x x
0 0 0 0 x x x x
0 0 1 0 x x x x
0 0 0 0 x x x x
0 0 1 0 x x x x
0 0 0 0 x x x x
0 0 1 0 x x x x
0 0 0 0 x x x x
0 0 1 0 x x x x
0 0 0 0 x x x x
0 0 1 0 x x x x
0 0 0 0 x x x x
0 0 1 0 x x x x
0 0 0 0 x x x x
0 0 1 0 x x x x
0 0 0 0 x x x x
0 0 1 0 x x x x
0 0 0 0 x x x x
0 0 1 0 x x x x
0 0 0 0 x x x x
0 0 1 0 x x x x
0 0 0 0 x x x x
0 0 1 0 x x x x
0 0 0 0 x x x x
0 0 1 0 x x x x
0 0 0 0 x x x x
0 0 1 0 x x x x
0 0 0 0 x x x x
0 0 1 0 x x x x
0 0 0 0 x x x x
0 0 1 0 x x x x
0 0 0 0 x x x x
0 0 1 0 x x x x
0 0 0 0 x x x x
0 0 1 0 x x x x
0 0 0 0 x x x x
0 0 1 0 x x x x
0 0 0 0 x x x x
0 0 1 0 x x x x
0 0 0 0 x x x x
0 0 1 0 x x x x
0 0 0 0 x x x x
0 0 1 0 x x x x
0 0 0 0 x x x x
0 0 1 0 x x x x
0 0 0 0 x x x x
0 0 1 0 x x x x
0 0 0 0 x x x x
0 0 1 0 x x x x
0 0 0 0 x x x x
0 0 1 0 x x x x
0 0 0 0 x x x x
0 0 1 0 x x x x
0 0 0 0 x x x x
0 0 1 0 x x x x
0 0 0 0 x x x x
0 0 1 0 x x x x
0 0 0 0 x x x x
0 0 1 0 x x x x
0 0 0 0 x x x x
0 0 1 0 x x x x
0 0 0 0 x x x x
0 0 1 0 x x x x
0 0 0 0 x x x x
0 0 1 0 x x x x
0 0 0 0 x x x x
0 0 1 0 x x x x
0 0 0 0 x x x x
0 0 1 0 x x x x
0 0 0 0 x x x x
0 0 1 0 x x x x
0 0 0 0 x x x x
0 0 1 0 x x x x
0 0 0 0 x x x x
0 0 1 0 x x x x
0 0 0 0 x x x x
0 0 1 0 x x x x
0 0 0 0 x x x x
0 0 1 0 x x x x
0 0 0 0 x x x x
0 0 1 0 x x x x
0 0 0 0 x x x x
0 0 1 0 x x x x
0 0 0 0 x x x x
0 0 1 0 x x x x
0 0 0 0 x x x x
0 0 1 0 x x x x
0 0 0 0 x x x x
0 0 1 0 x x x x
0 0 0 0 x x x x
0 0 1 0 x x x x
0 0 0 0 x x x x
0 0 1 0 x x x x
0 0 0 0 x x x x
0 0 1 0 x x x x
0 0 0 0 x x x x
0 0 1 0 x x x x
0 0 0 0 x x x x
0 0 1 0 x x x x
0 0 0 0 x x x x
0 0 1 0 x x x x
0 0 0 0 x x x x
0 0 1 0 x x x x
0 0 0 0 x x x x
0 0 1 0 x x x x
0 0 0 0 x x x x
0 0 1 0 x x x x
0 0 0 0 x x x x
0 0 1 0 x x x x
0 0 0 0 x x x x
0 0 1 0 x x x x
0 0 0 0 x x x x
0 0 1 0 x x x x
0 0 0 0 x x x x
0 0 1 0 x x x x
0 0 0 0 x x x x
0 0 1 0 x x x x
0 0 0 0 x x x x
0 0 1 0 x x x x
0 0 0 0 x x x x
0 0 1 0 x x x x
0 0 0 0 x x x x
0 0 1 0 x x x x
0 0 0 0 x x x x
0 0 1 0 x x x x
0 0 0 0 x x x x
0 0 1 0 x x x x
0 0 0 0 x x x x
0 0 1 0 x x x x
0 0 0 0 x x x x
0 0 1 0 x x x x
0 0 0 0 x x x x
0 0 1 0 x x x x
0 0 0 0 x x x x
0 0 1 0 x x x x
0 0 0 0 x x x x
0 0 1 0 x x x x
0 0 0 0 x x x x
0 0 1 0 x x x x
0 0 0 0 x x x x
0 0 1 0 x x x x
0 0 0 0 x x x x
0 0 1 0 x x x x
0 0 0 0 x x x x
0 0 1 0 x x x x
0 0 0 0 x x x x
0 0 1 0 x x x x
0 0 0 0 x x x x
0 0 1 0 x x x x
0 0 0 0 x x x x
0 0 1 0 x x x x
0 0 0 0 x x x x
0 0 1 0 x x x x
0 0 0 0 x x x x
0 0 1 0 x x x x
0 0 0 0 x x x x
0 0 1 0 x x x x
0 0 0 0 x x x x
0 0 1 0 x x x x
0 0 0 0 x x x x
0 0 1 0 x x x x
0 0 0 0 x x x x
0 0 1 0 x x x x
0 0 0 0 x x x x
0 0 1 0 x x x x
0 0 0 0 x x x x
0 0 1 0 x x x x
0 0 0 0 x x x x
0 0 1 0 x x x x
0 0 0 0 x x x x
0 0 1 0 x x x x
0 0 0 0 x x x x
0 0 1 0 x x x x
0 0 0 0 x x x x
0 0 1 0 x x x x
0 0 0 0 x x x x
0 0 1 0 x x x x
0 0 0 0 x x x x
0 0 1 0 x x x x
0 0 0 0 x x x x
0 0 1 0 x x x x
0 0 0 0 x x x x
0 0 1 0 x x x x
0 0 0 0 x x x x
0 0 1 0 x x x x
0 0 0 0 x x x x
0 0 1 0 x x x x
0 0 0 0 x x x x
0 0 1 0 x x x x
0 0 0 0 x x x x
0 0 1 0 x x x x
0 0 0 0 x x x x
0 0 1 0 x x x x
0 0 0 0 x x x x
0 0 1 0 x x x x
0 0 0 0 x x x x
0 0 1 0 x x x x
0 0 0 0 x x x x
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*/
