// Digital circuit 01.dig as structural Verilog
module _01 (
  input  reset,
  input  X,
  input  Y,
  input  Z,
  input  load,
  input  clock,
  output A,
  output B,
  output C
);

  wire [2:0] lookuptable_1_out, multiplexer_1_out, multiplexer_2_out;

  LookUpTable #(.Bits(3)) lookuptable_1 (.in0(C), .in1(B), .in2(A), .out(lookuptable_1_out));
  Multiplexer #(.Bits(3)) multiplexer_1 (
    .sel(load), .in_0(lookuptable_1_out), .in_1({X, Y, Z}), .out(multiplexer_1_out));
  Multiplexer #(.Bits(3)) multiplexer_2 (.sel(reset), .in_0(multiplexer_1_out), .in_1(3'b010), .out(multiplexer_2_out));
  D_FF #(.Bits(3)) d_ff_1 (.D(multiplexer_2_out), .C(clock), .Q({A, B, C}));  // open: nQ

  // Notes on the sheet:
  //   contents of lookuptable_1 (hex, n*v repeats v):
  //   7,7,6,0,2,6,3,4
endmodule

/* Test case T01:
X Y Z reset load clock A B C
0 0 0 1     0    0     x x x
0 0 0 1     0    1     0 1 0
1 1 0 0     1    0     0 1 0
1 1 0 0     1    1     1 1 0
0 0 0 0     0    0     1 1 0
0 0 0 0     0    1     0 1 1
0 0 0 0     0    0     0 1 1
0 0 0 0     0    1     0 0 0
0 0 0 0     0    0     0 0 0
0 0 0 0     0    1     1 1 1
0 0 0 0     0    0     1 1 1
0 0 0 0     0    1     1 0 0
0 0 0 0     0    0     1 0 0
0 0 0 0     0    1     0 1 0
0 0 0 0     0    0     0 1 0
0 0 0 0     0    1     1 1 0
0 0 0 0     0    0     1 1 0
0 0 0 0     0    1     0 1 1
0 0 0 0     0    0     0 1 1
0 0 0 0     0    1     0 0 0
0 0 0 0     0    0     0 0 0
*/
