// Digital circuit 02.dig as structural Verilog
module _02 (
  input  reset,
  input  [7:0] M,
  input  start,
  input  clock,
  input  [7:0] N,
  output [15:0] Z,
  output [15:0] out_7,
  output busy,
  output [15:0] out_9
);

  wire and_1_out, and_3_out, and_4_out, and_5_out, comparator_1_eq, comparator_1_gt, comparator_1_lt,
       d_ff_1_q, multiplexer_1_out, or_1_out, or_2_out, run;
  wire [15:0] add_1_s, add_2_s, add_3_s, currN, div_1_r, m__plus__2, multiplexer_2_out, multiplexer_3_out,
       multiplexer_4_out, multiplexer_6_out, multiplexer_7_out, multiplexer_8_out, sum;

  Div #(.Bits(16)) div_1 (.a({{8{1'b0}}, M}), .b(16'h2), .r(div_1_r));  // open: q
  Add #(.Bits(16)) add_1 (.a({{8{1'b0}}, M}), .b(16'h1), .c_i(1'b0), .s(add_1_s));  // open: c_o
  Multiplexer multiplexer_1 (.sel(reset), .in_0(start), .in_1(1'b0), .out(multiplexer_1_out));
  Multiplexer #(.Bits(16)) multiplexer_2 (
    .sel(div_1_r[0]), .in_0({{8{1'b0}}, M}), .in_1(add_1_s), .out(multiplexer_2_out));
  D_FF d_ff_1 (.D(multiplexer_1_out), .C(clock), .Q(d_ff_1_q));  // open: nQ
  Multiplexer #(.Bits(16)) multiplexer_3 (
    .sel(run), .in_0(m__plus__2), .in_1(multiplexer_2_out), .out(multiplexer_3_out));
  Comparator #(.Bits(16)) comparator_1 (
    .a(out_7), .b(currN), .gt(comparator_1_gt), .eq(comparator_1_eq), .lt(comparator_1_lt));
  and and_1 (and_1_out, ~d_ff_1_q, start);  // And
  D_FF #(.Bits(16)) d_ff_2 (.D(multiplexer_3_out), .C(clock), .Q(out_7));  // open: nQ
  or or_1 (or_1_out, comparator_1_eq, comparator_1_lt);
  and and_2 (run, ~busy, and_1_out);  // And
  and and_3 (and_3_out, busy, or_1_out);
  and and_4 (and_4_out, or_1_out, busy);
  or or_2 (or_2_out, and_3_out, run);
  Add #(.Bits(16)) add_2 (.a(out_7), .b(16'h2), .c_i(1'b0), .s(add_2_s));  // open: c_o
  Multiplexer #(.Bits(16)) multiplexer_4 (.sel(comparator_1_gt), .in_0(Z), .in_1(out_9), .out(multiplexer_4_out));
  and and_5 (and_5_out, ~reset, or_2_out);  // And
  Multiplexer #(.Bits(16)) multiplexer_5 (.sel(and_4_out), .in_0(out_7), .in_1(add_2_s), .out(m__plus__2));
  Multiplexer #(.Bits(16)) multiplexer_6 (.sel(run), .in_0(sum), .in_1({16{1'b0}}), .out(multiplexer_6_out));
  Multiplexer #(.Bits(16)) multiplexer_7 (.sel(run), .in_0(currN), .in_1({{8{1'b0}}, N}), .out(multiplexer_7_out));
  Multiplexer #(.Bits(16)) multiplexer_8 (
    .sel(reset), .in_0(multiplexer_4_out), .in_1({16{1'b0}}), .out(multiplexer_8_out));
  D_FF #(.Bits(16)) d_ff_3 (.D(multiplexer_6_out), .C(clock), .Q(out_9));  // open: nQ
  D_FF #(.Bits(16)) d_ff_4 (.D(multiplexer_7_out), .C(clock), .Q(currN));  // open: nQ
  D_FF #(.Bits(16)) d_ff_5 (.D(multiplexer_8_out), .C(clock), .Q(Z));  // open: nQ
  D_FF d_ff_6 (.D(and_5_out), .C(clock), .Q(busy));  // open: nQ
  Add #(.Bits(16)) add_3 (.a(out_9), .b(out_7), .c_i(1'b0), .s(add_3_s));  // open: c_o
  Multiplexer #(.Bits(16)) multiplexer_9 (.sel(and_4_out), .in_0(out_9), .in_1(add_3_s), .out(sum));

  // Other names for the same wires on the sheet: clk = clock; currM[15:0] = out_7; currSum[15:0] = out_9;
  //   m_t[7:0] = M; n_t[7:0] = N
endmodule

/* Test case T01:
 M  N start clock reset Z busy
 0  0 0     0     1     x x
 0  0 0     1     1     x 0
 0  0 0     0     1     x 0
 0  0 0     1     1     x 0
 1 10 1     0     0     x 0
 1 10 1     1     0     x 1
 0  0 0     0     0     x 1
 0  0 0     1     0     x 1
 0  0 0     0     0     x 1
 0  0 0     1     0     x 1
 0  0 0     0     0     x 1
 0  0 0     1     0     x x
 0  0 0     0     0     x x
 0  0 0     1     0     x x
 0  0 0     0     0     x x
 0  0 0     1     0     x x
 0  0 0     0     0     x x
 0  0 0     1     0     x x
 0  0 0     0     0     x x
 0  0 0     1     0     x x
 0  0 0     0     0     x x
 0  0 0     1     0     x x
 0  0 0     0     0     x x
 0  0 0     1     0     x x
 0  0 0     0     0     x x
 0  0 0     1     0     x x
 0  0 0     0     0     x x
 0  0 0     1     0     x x
 0  0 0     0     0     x x
 0  0 0     1     0     x x
 0  0 0     0     0     x x
 0  0 0     1     0     x x
 0  0 0     0     0     x x
 0  0 0     1     0     x x
 0  0 0     0     0     x x
 0  0 0     1     0     x x
 0  0 0     0     0     x x
 0  0 0     1     0     x x
 0  0 0     0     0     x x
 0  0 0     1     0     x x
 0  0 0     0     0     x x
 0  0 0     1     0     x x
 0  0 0     0     0     x x
 0  0 0     1     0     x x
 0  0 0     0     0     x x
 0  0 0     1     0     x x
 0  0 0     0     0     x x
 0  0 0     1     0     x x
 0  0 0     0     0     x x
 0  0 0     1     0     x x
 0  0 0     0     0     x x
 0  0 0     1     0     x x
 0  0 0     0     0     x x
 0  0 0     1     0     x x
 0  0 0     0     0     x x
 0  0 0     1     0     x x
 0  0 0     0     0     x x
 0  0 0     1     0     x x
 0  0 0     0     0     x x
 0  0 0     1     0     x x
 0  0 0     0     0     x x
 0  0 0     1     0     x x
 0  0 0     0     0     x x
 0  0 0     1     0     x x
 0  0 0     0     0     x x
 0  0 0     1     0     x x
 0  0 0     0     0     x x
 0  0 0     1     0     x x
 0  0 0     0     0     x x
 0  0 0     1     0     x x
 0  0 0     0     0     x x
 0  0 0     1     0     x x
 0  0 0     0     0     x x
 0  0 0     1     0     x x
 0  0 0     0     0     x x
 0  0 0     1     0     x x
 0  0 0     0     0     x x
 0  0 0     1     0     x x
 0  0 0     0     0     x x
 0  0 0     1     0     x x
 0  0 0     0     0     x x
 0  0 0     1     0     x x
 0  0 0     0     0     x x
 0  0 0     1     0     x x
 0  0 0     0     0     x x
 0  0 0     1     0     x x
 0  0 0     0     0     x x
 0  0 0     1     0     x x
 0  0 0     0     0     x x
 0  0 0     1     0     x x
 0  0 0     0     0     x x
 0  0 0     1     0     x x
 0  0 0     0     0     x x
 0  0 0     1     0     x x
 0  0 0     0     0     x x
 0  0 0     1     0     x x
 0  0 0     0     0     x x
 0  0 0     1     0     x x
 0  0 0     0     0     x x
 0  0 0     1     0     x x
 0  0 0     0     0     x x
 0  0 0     1     0     x x
 0  0 0     0     0     x x
 0  0 0     1     0     x x
 0  0 0     0     0     x x
 0  0 0     1     0     x x
 0  0 0     0     0     x x
 0  0 0     1     0     x x
 0  0 0     0     0     x x
 0  0 0     1     0     x x
 0  0 0     0     0     x x
 0  0 0     1     0     x x
 0  0 0     0     0     x x
 0  0 0     1     0     x x
 0  0 0     0     0     30 0
 0  0 0     1     0     30 0
 0  0 0     0     0     30 0
 0  0 0     1     0     30 0
*/
