// Digital circuit 03.dig as structural Verilog
module _03 (
  input  reset,
  input  [3:0] N,
  input  \new ,
  input  clock,
  output [7:0] num3,
  output busy,
  output [7:0] num5
);

  wire and_1_out, and_2_out, and_3_out, comparator_1_eq, comparator_2_eq, d_ff_1_q, multiplexer_1_out, run;
  wire [7:0] counter_1_out, counter_2_out, div_1_r, div_2_r, multiplexer_2_out, multiplexer_3_out;

  Multiplexer multiplexer_1 (.sel(reset), .in_0(\new ), .in_1(1'b0), .out(multiplexer_1_out));
  Div #(.Bits(8)) div_1 (.a({4'b0000, N}), .b(8'h3), .r(div_1_r));  // open: q
  Div #(.Bits(8)) div_2 (.a({4'b0000, N}), .b(8'h5), .r(div_2_r));  // open: q
  D_FF d_ff_1 (.D(multiplexer_1_out), .C(clock), .Q(d_ff_1_q));  // open: nQ
  Comparator #(.Bits(8)) comparator_1 (.a(div_1_r), .b({8{1'b0}}), .eq(comparator_1_eq));  // open: gt, lt
  Comparator #(.Bits(8)) comparator_2 (.a(div_2_r), .b({8{1'b0}}), .eq(comparator_2_eq));  // open: gt, lt
  and and_1 (and_1_out, ~d_ff_1_q, \new );  // And
  and and_2 (and_2_out, run, comparator_1_eq);
  and and_3 (and_3_out, run, comparator_2_eq);
  and and_4 (run, ~busy, and_1_out);  // And
  Counter #(.Bits(8)) counter_1 (.en(and_2_out), .C(clock), .clr(reset), .out(counter_1_out));  // open: ovf
  Counter #(.Bits(8)) counter_2 (.en(and_3_out), .C(clock), .clr(reset), .out(counter_2_out));  // open: ovf
  D_FF d_ff_2 (.D(run), .C(clock), .Q(busy));  // open: nQ
  Multiplexer #(.Bits(8)) multiplexer_2 (.sel(reset), .in_0(counter_1_out), .in_1({8{1'b0}}), .out(multiplexer_2_out));
  Multiplexer #(.Bits(8)) multiplexer_3 (.sel(reset), .in_0(counter_2_out), .in_1({8{1'b0}}), .out(multiplexer_3_out));
  D_FF #(.Bits(8)) d_ff_3 (.D(multiplexer_2_out), .C(clock), .Q(num3));  // open: nQ
  D_FF #(.Bits(8)) d_ff_4 (.D(multiplexer_3_out), .C(clock), .Q(num5));  // open: nQ

  // Other names for the same wires on the sheet: clk = clock; n_t[3:0] = N
endmodule

/* Test case T01:
 N new reset clock num3 num5 busy
 0 0   1     0     x    x    x
 0 0   1     1     x    x    x
14 1   0     0     0    0    x
14 1   0     1     0    0    1
 0 0   0     0     x    x    1
 0 0   0     1     x    x    x
 0 0   0     0     x    x    x
 0 0   0     1     x    x    x
 0 0   0     0     x    x    x
 0 0   0     1     x    x    x
 0 0   0     0     x    x    x
 0 0   0     1     x    x    x
 0 0   0     0     x    x    x
 0 0   0     1     x    x    x
 0 0   0     0     x    x    x
 0 0   0     1     x    x    x
 0 0   0     0     x    x    x
 0 0   0     1     x    x    x
 0 0   0     0     x    x    x
 0 0   0     1     x    x    x
 0 0   0     0     x    x    x
 0 0   0     1     x    x    x
 0 0   0     0     x    x    x
 0 0   0     1     x    x    x
 0 0   0     0     0    0    0
 0 0   0     1     0    0    0
15 1   0     0     0    0    x
15 1   0     1     0    0    1
 0 0   0     0     x    x    1
 0 0   0     1     x    x    x
 0 0   0     0     x    x    x
 0 0   0     1     x    x    x
 0 0   0     0     x    x    x
 0 0   0     1     x    x    x
 0 0   0     0     x    x    x
 0 0   0     1     x    x    x
 0 0   0     0     x    x    x
 0 0   0     1     x    x    x
 0 0   0     0     x    x    x
 0 0   0     1     x    x    x
 0 0   0     0     x    x    x
 0 0   0     1     x    x    x
 0 0   0     0     x    x    x
 0 0   0     1     x    x    x
 0 0   0     0     x    x    x
 0 0   0     1     x    x    x
 0 0   0     0     x    x    x
 0 0   0     1     x    x    x
 0 0   0     0     1    1    0
 0 0   0     1     1    1    0
*/
