// Digital circuit 02_06.dig as structural Verilog
module _02_06 (
  input  A,
  input  B,
  input  C,
  input  D,
  output Z1,
  output Z2,
  output Z3
);

  wire and_1_out, and_2_out, and_3_out, and_4_out, and_5_out, and_6_out, and_7_out, and_8_out, and_10_out,
       and_11_out, and_12_out, and_13_out, and_14_out, and_15_out, and_16_out, and_17_out, and_19_out,
       and_20_out, and_21_out, and_22_out, and_23_out, and_24_out, and_25_out, and_26_out, and_27_out,
       and_28_out, not_1_out, not_2_out, not_3_out, not_4_out, not_5_out, not_6_out, not_7_out, not_8_out,
       not_9_out, not_10_out, not_11_out, not_12_out, not_13_out, not_14_out, not_15_out, not_16_out,
       not_17_out, not_18_out, not_19_out, not_20_out, not_21_out, not_22_out, not_23_out, not_24_out,
       not_25_out, not_26_out, not_27_out, not_28_out, not_29_out, not_30_out, not_31_out, not_32_out,
       not_33_out, not_34_out, not_35_out, not_36_out, not_37_out, not_38_out, not_39_out, not_40_out,
       not_41_out, not_42_out, not_43_out, not_44_out, not_45_out, not_46_out, not_47_out, not_48_out,
       not_49_out, not_50_out, not_51_out, not_52_out, not_53_out, not_54_out, not_55_out, not_56_out,
       not_57_out, not_58_out, not_59_out, not_60_out, not_61_out, not_62_out, not_63_out, not_64_out,
       or_1_out, or_2_out, or_3_out, or_4_out, or_5_out, or_6_out, or_7_out, or_8_out, or_9_out, or_10_out,
       or_11_out, or_12_out, or_13_out, or_14_out, or_15_out, or_16_out, or_17_out, or_18_out, or_19_out,
       or_20_out, or_21_out, or_22_out, or_23_out, or_24_out, or_25_out, or_26_out, or_27_out, or_28_out,
       or_29_out, or_30_out, or_31_out, or_32_out, or_33_out, or_34_out, or_35_out, or_36_out, or_37_out,
       or_38_out, or_39_out, or_40_out, or_41_out, or_42_out, or_43_out, or_44_out, or_45_out, or_46_out,
       or_47_out, or_48_out, or_49_out, or_50_out, or_51_out, or_52_out, or_53_out, or_54_out, or_55_out,
       or_56_out, or_57_out, or_58_out, or_59_out, or_60_out, or_61_out, or_62_out, or_63_out, or_64_out,
       or_65_out, or_66_out, or_67_out, or_68_out, or_69_out, or_70_out, or_71_out, or_72_out, or_73_out,
       or_74_out, or_75_out, or_76_out, or_77_out, or_78_out, or_79_out, or_80_out, or_81_out, or_82_out,
       or_83_out, or_84_out, or_85_out, or_86_out, or_87_out, or_88_out, or_89_out, or_90_out, or_91_out,
       or_92_out, or_93_out, or_94_out, or_95_out, or_96_out;

  not not_1 (not_1_out, D);
  not not_2 (not_2_out, C);
  not not_3 (not_3_out, C);
  not not_4 (not_4_out, D);
  not not_5 (not_5_out, B);
  not not_6 (not_6_out, D);
  not not_7 (not_7_out, B);
  not not_8 (not_8_out, C);
  not not_9 (not_9_out, B);
  not not_10 (not_10_out, C);
  not not_11 (not_11_out, D);
  not not_12 (not_12_out, A);
  not not_13 (not_13_out, C);
  not not_14 (not_14_out, A);
  not not_15 (not_15_out, C);
  not not_16 (not_16_out, D);
  not not_17 (not_17_out, A);
  not not_18 (not_18_out, B);
  not not_19 (not_19_out, C);
  not not_20 (not_20_out, D);
  or or_1 (or_1_out, A, B);
  or or_2 (or_2_out, C, D);
  or or_3 (or_3_out, A, B);
  or or_4 (or_4_out, C, not_1_out);
  or or_5 (or_5_out, A, B);
  or or_6 (or_6_out, not_2_out, D);
  or or_7 (or_7_out, A, B);
  or or_8 (or_8_out, not_3_out, not_4_out);
  or or_9 (or_9_out, A, not_5_out);
  or or_10 (or_10_out, C, not_6_out);
  or or_11 (or_11_out, A, not_7_out);
  or or_12 (or_12_out, not_8_out, D);
  or or_13 (or_13_out, A, not_9_out);
  or or_14 (or_14_out, not_10_out, not_11_out);
  or or_15 (or_15_out, not_12_out, B);
  or or_16 (or_16_out, not_13_out, D);
  or or_17 (or_17_out, not_14_out, B);
  or or_18 (or_18_out, not_15_out, not_16_out);
  or or_19 (or_19_out, not_17_out, not_18_out);
  or or_20 (or_20_out, not_19_out, not_20_out);
  or or_21 (or_21_out, or_1_out, or_2_out);
  or or_22 (or_22_out, or_3_out, or_4_out);
  or or_23 (or_23_out, or_5_out, or_6_out);
  or or_24 (or_24_out, or_7_out, or_8_out);
  or or_25 (or_25_out, or_9_out, or_10_out);
  or or_26 (or_26_out, or_11_out, or_12_out);
  or or_27 (or_27_out, or_13_out, or_14_out);
  or or_28 (or_28_out, or_15_out, or_16_out);
  or or_29 (or_29_out, or_17_out, or_18_out);
  or or_30 (or_30_out, or_19_out, or_20_out);
  and and_1 (and_1_out, or_21_out, or_22_out);
  and and_2 (and_2_out, or_23_out, or_24_out);
  and and_3 (and_3_out, or_25_out, or_26_out);
  and and_4 (and_4_out, or_27_out, or_28_out);
  and and_5 (and_5_out, or_29_out, or_30_out);
  and and_6 (and_6_out, and_1_out, and_2_out);
  and and_7 (and_7_out, and_3_out, and_4_out);
  and and_8 (and_8_out, and_6_out, and_7_out);
  and and_9 (Z1, and_8_out, and_5_out);
  not not_21 (not_21_out, B);
  not not_22 (not_22_out, B);
  not not_23 (not_23_out, D);
  not not_24 (not_24_out, A);
  not not_25 (not_25_out, A);
  not not_26 (not_26_out, D);
  not not_27 (not_27_out, A);
  not not_28 (not_28_out, C);
  not not_29 (not_29_out, A);
  not not_30 (not_30_out, B);
  not not_31 (not_31_out, A);
  not not_32 (not_32_out, B);
  not not_33 (not_33_out, D);
  not not_34 (not_34_out, A);
  not not_35 (not_35_out, B);
  not not_36 (not_36_out, C);
  not not_37 (not_37_out, A);
  not not_38 (not_38_out, B);
  not not_39 (not_39_out, C);
  not not_40 (not_40_out, D);
  or or_31 (or_31_out, A, B);
  or or_32 (or_32_out, C, D);
  or or_33 (or_33_out, A, not_21_out);
  or or_34 (or_34_out, C, D);
  or or_35 (or_35_out, A, not_22_out);
  or or_36 (or_36_out, C, not_23_out);
  or or_37 (or_37_out, not_24_out, B);
  or or_38 (or_38_out, C, D);
  or or_39 (or_39_out, not_25_out, B);
  or or_40 (or_40_out, C, not_26_out);
  or or_41 (or_41_out, not_27_out, B);
  or or_42 (or_42_out, not_28_out, D);
  or or_43 (or_43_out, not_29_out, not_30_out);
  or or_44 (or_44_out, C, D);
  or or_45 (or_45_out, not_31_out, not_32_out);
  or or_46 (or_46_out, C, not_33_out);
  or or_47 (or_47_out, not_34_out, not_35_out);
  or or_48 (or_48_out, not_36_out, D);
  or or_49 (or_49_out, not_37_out, not_38_out);
  or or_50 (or_50_out, not_39_out, not_40_out);
  or or_51 (or_51_out, or_31_out, or_32_out);
  or or_52 (or_52_out, or_33_out, or_34_out);
  or or_53 (or_53_out, or_35_out, or_36_out);
  or or_54 (or_54_out, or_37_out, or_38_out);
  or or_55 (or_55_out, or_39_out, or_40_out);
  or or_56 (or_56_out, or_41_out, or_42_out);
  or or_57 (or_57_out, or_43_out, or_44_out);
  or or_58 (or_58_out, or_45_out, or_46_out);
  or or_59 (or_59_out, or_47_out, or_48_out);
  or or_60 (or_60_out, or_49_out, or_50_out);
  and and_10 (and_10_out, or_51_out, or_52_out);
  and and_11 (and_11_out, or_53_out, or_54_out);
  and and_12 (and_12_out, or_55_out, or_56_out);
  and and_13 (and_13_out, or_57_out, or_58_out);
  and and_14 (and_14_out, or_59_out, or_60_out);
  and and_15 (and_15_out, and_10_out, and_11_out);
  and and_16 (and_16_out, and_12_out, and_13_out);
  and and_17 (and_17_out, and_15_out, and_16_out);
  and and_18 (Z2, and_17_out, and_14_out);
  or or_61 (or_61_out, A, B);
  or or_62 (or_62_out, C, not_41_out);
  not not_41 (not_41_out, D);
  or or_63 (or_63_out, A, B);
  or or_64 (or_64_out, not_42_out, D);
  not not_42 (not_42_out, C);
  or or_65 (or_65_out, A, B);
  or or_66 (or_66_out, not_43_out, not_44_out);
  not not_43 (not_43_out, C);
  not not_44 (not_44_out, D);
  or or_67 (or_67_out, A, not_45_out);
  not not_45 (not_45_out, B);
  or or_68 (or_68_out, C, D);
  or or_69 (or_69_out, A, not_46_out);
  not not_46 (not_46_out, B);
  or or_70 (or_70_out, not_47_out, D);
  not not_47 (not_47_out, C);
  or or_71 (or_71_out, A, not_48_out);
  not not_48 (not_48_out, B);
  or or_72 (or_72_out, not_49_out, not_50_out);
  not not_49 (not_49_out, C);
  not not_50 (not_50_out, D);
  or or_73 (or_73_out, not_51_out, B);
  not not_51 (not_51_out, A);
  or or_74 (or_74_out, C, D);
  or or_75 (or_75_out, not_52_out, B);
  not not_52 (not_52_out, A);
  or or_76 (or_76_out, C, not_53_out);
  not not_53 (not_53_out, D);
  or or_77 (or_77_out, not_54_out, B);
  not not_54 (not_54_out, A);
  or or_78 (or_78_out, not_55_out, not_56_out);
  not not_55 (not_55_out, C);
  not not_56 (not_56_out, D);
  or or_79 (or_79_out, not_57_out, not_58_out);
  not not_57 (not_57_out, A);
  not not_58 (not_58_out, B);
  or or_80 (or_80_out, C, D);
  or or_81 (or_81_out, not_59_out, not_60_out);
  not not_59 (not_59_out, A);
  not not_60 (not_60_out, B);
  or or_82 (or_82_out, C, not_61_out);
  not not_61 (not_61_out, D);
  or or_83 (or_83_out, not_62_out, not_63_out);
  not not_62 (not_62_out, A);
  not not_63 (not_63_out, B);
  or or_84 (or_84_out, not_64_out, D);
  not not_64 (not_64_out, C);
  or or_85 (or_85_out, or_61_out, or_62_out);
  or or_86 (or_86_out, or_63_out, or_64_out);
  or or_87 (or_87_out, or_65_out, or_66_out);
  or or_88 (or_88_out, or_67_out, or_68_out);
  or or_89 (or_89_out, or_69_out, or_70_out);
  or or_90 (or_90_out, or_71_out, or_72_out);
  or or_91 (or_91_out, or_73_out, or_74_out);
  or or_92 (or_92_out, or_75_out, or_76_out);
  or or_93 (or_93_out, or_77_out, or_78_out);
  or or_94 (or_94_out, or_79_out, or_80_out);
  or or_95 (or_95_out, or_81_out, or_82_out);
  or or_96 (or_96_out, or_83_out, or_84_out);
  and and_19 (and_19_out, or_85_out, or_86_out);
  and and_20 (and_20_out, or_87_out, or_88_out);
  and and_21 (and_21_out, or_89_out, or_90_out);
  and and_22 (and_22_out, or_91_out, or_92_out);
  and and_23 (and_23_out, or_93_out, or_94_out);
  and and_24 (and_24_out, or_95_out, or_96_out);
  and and_25 (and_25_out, and_19_out, and_20_out);
  and and_26 (and_26_out, and_21_out, and_22_out);
  and and_27 (and_27_out, and_23_out, and_24_out);
  and and_28 (and_28_out, and_25_out, and_26_out);
  and and_29 (Z3, and_28_out, and_27_out);
endmodule
