// Digital circuit 02_07.dig as structural Verilog
module _02_07 (
  input  X0,
  input  X1,
  input  Selector,
  output Z
);

  wire and_1_out, and_2_out, and_3_out, and_4_out, and_5_out, and_6_out, and_7_out, and_8_out, not_1_out,
       not_2_out, not_3_out, not_4_out, or_1_out, or_2_out;

  and and_1 (and_1_out, not_1_out, X1);
  not not_1 (not_1_out, X0);
  and and_2 (and_2_out, X0, not_2_out);
  not not_2 (not_2_out, X1);
  and and_3 (and_3_out, X0, X1);
  and and_4 (and_4_out, X0, X1);
  and and_5 (and_5_out, and_1_out, Selector);
  and and_6 (and_6_out, and_2_out, not_3_out);
  not not_3 (not_3_out, Selector);
  and and_7 (and_7_out, and_3_out, not_4_out);
  not not_4 (not_4_out, Selector);
  and and_8 (and_8_out, and_4_out, Selector);
  or or_1 (or_1_out, and_5_out, and_6_out);
  or or_2 (or_2_out, and_7_out, and_8_out);
  or or_3 (Z, or_1_out, or_2_out);
endmodule
