// Digital circuit 02_08.dig as structural Verilog
module _02_08 (
  input  X0,
  input  X1,
  input  Selector,
  output Z
);

  wire and_1_out, and_2_out, not_1_out, not_2_out, not_3_out, not_4_out, or_1_out, or_2_out, or_3_out,
       or_4_out, or_5_out, or_6_out, or_7_out, or_8_out;

  or or_1 (or_1_out, X0, X1);
  or or_2 (or_2_out, X0, X1);
  or or_3 (or_3_out, X0, not_1_out);
  not not_1 (not_1_out, X1);
  or or_4 (or_4_out, not_2_out, X1);
  not not_2 (not_2_out, X0);
  or or_5 (or_5_out, or_1_out, Selector);
  or or_6 (or_6_out, or_2_out, not_3_out);
  not not_3 (not_3_out, Selector);
  or or_7 (or_7_out, or_3_out, Selector);
  or or_8 (or_8_out, or_4_out, not_4_out);
  not not_4 (not_4_out, Selector);
  and and_1 (and_1_out, or_5_out, or_6_out);
  and and_2 (and_2_out, or_7_out, or_8_out);
  and and_3 (Z, and_1_out, and_2_out);
endmodule
