// Digital circuit 02_09.dig as structural Verilog
module _02_09 (
  input  X0,
  input  X1,
  input  X2,
  input  X3,
  input  S0,
  input  S1,
  output Z
);

  wire and_1_out, and_2_out, and_3_out, and_4_out, and_5_out, and_6_out, and_7_out, and_8_out, and_9_out,
       and_10_out, and_11_out, and_12_out, and_13_out, and_14_out, and_15_out, and_16_out, and_17_out,
       and_18_out, and_19_out, and_20_out, and_21_out, and_22_out, and_23_out, and_24_out, not_1_out,
       not_2_out, not_3_out, not_4_out, not_5_out, not_6_out, not_7_out, not_8_out, not_9_out, not_10_out,
       not_11_out, not_12_out, or_1_out, or_2_out, or_3_out, or_4_out, or_5_out, or_6_out, or_7_out, or_8_out;

  not not_1 (not_1_out, X0);
  not not_2 (not_2_out, X1);
  not not_3 (not_3_out, X2);
  not not_4 (not_4_out, X3);
  and and_1 (and_1_out, not_1_out, X1);
  and and_2 (and_2_out, X0, not_2_out);
  not not_5 (not_5_out, S0);
  and and_3 (and_3_out, X0, X1);
  not not_6 (not_6_out, S0);
  and and_4 (and_4_out, X0, X1);
  and and_5 (and_5_out, not_3_out, X3);
  and and_6 (and_6_out, X2, not_4_out);
  not not_7 (not_7_out, S0);
  and and_7 (and_7_out, X2, X3);
  not not_8 (not_8_out, S0);
  and and_8 (and_8_out, X2, X3);
  and and_9 (and_9_out, and_1_out, S0);
  and and_10 (and_10_out, and_2_out, not_5_out);
  and and_11 (and_11_out, and_3_out, not_6_out);
  and and_12 (and_12_out, and_4_out, S0);
  and and_13 (and_13_out, and_5_out, S0);
  and and_14 (and_14_out, and_6_out, not_7_out);
  and and_15 (and_15_out, and_7_out, not_8_out);
  and and_16 (and_16_out, and_8_out, S0);
  or or_1 (or_1_out, and_9_out, and_10_out);
  or or_2 (or_2_out, and_11_out, and_12_out);
  or or_3 (or_3_out, and_13_out, and_14_out);
  or or_4 (or_4_out, and_15_out, and_16_out);
  or or_5 (or_5_out, or_1_out, or_2_out);
  or or_6 (or_6_out, or_3_out, or_4_out);
  and and_17 (and_17_out, not_9_out, or_6_out);
  not not_9 (not_9_out, or_5_out);
  and and_18 (and_18_out, or_5_out, not_10_out);
  not not_10 (not_10_out, or_6_out);
  and and_19 (and_19_out, or_5_out, or_6_out);
  and and_20 (and_20_out, or_5_out, or_6_out);
  and and_21 (and_21_out, and_17_out, S1);
  and and_22 (and_22_out, and_18_out, not_11_out);
  not not_11 (not_11_out, S1);
  and and_23 (and_23_out, and_19_out, not_12_out);
  not not_12 (not_12_out, S1);
  and and_24 (and_24_out, and_20_out, S1);
  or or_7 (or_7_out, and_21_out, and_22_out);
  or or_8 (or_8_out, and_23_out, and_24_out);
  or or_9 (Z, or_7_out, or_8_out);
endmodule
