// Digital circuit 03_03.dig as structural Verilog
module _03_03 (
  input  [3:0] In,
  input  [1:0] Selector,
  output [3:0] Output
);

  wire _20, _21, _22, _60, _61, _62, and_1_out, and_2_out, and_3_out, and_4_out, and_5_out, and_6_out,
       and_7_out, and_8_out, and_9_out, and_10_out, and_11_out, and_12_out, and_13_out, and_14_out,
       and_15_out, and_16_out, and_17_out, and_18_out, and_19_out, and_20_out, and_21_out, and_22_out,
       and_23_out, and_24_out, C1, C2, C3, E0, E1, E2, E3, not_1_out, not_2_out, not_3_out, not_4_out,
       not_5_out, not_6_out, not_8_out, not_9_out, not_10_out, not_11_out, not_12_out, not_13_out,
       not_14_out, not_15_out, not_16_out, not_17_out, not_18_out, not_19_out;

  not not_1 (not_1_out, In[2]);
  not not_2 (not_2_out, In[2]);
  not not_3 (not_3_out, In[1]);
  not not_4 (not_4_out, In[0]);
  and and_1 (and_1_out, In[2], In[0]);
  and and_2 (and_2_out, In[2], In[1]);
  and and_3 (and_3_out, not_1_out, In[1]);
  and and_4 (and_4_out, not_2_out, In[0]);
  and and_5 (and_5_out, In[2], not_3_out, not_4_out);
  or or_1 (E0, In[3], and_1_out, and_2_out);
  or or_2 (E1, and_3_out, and_4_out, and_5_out);
  not not_5 (not_5_out, In[1]);
  not not_6 (not_6_out, In[0]);
  and and_6 (and_6_out, not_5_out, not_6_out);
  and and_7 (and_7_out, In[1], In[0]);
  or or_3 (E2, and_6_out, and_7_out);
  not not_7 (E3, In[0]);
  and and_8 (and_8_out, not_8_out, In[1]);
  not not_8 (not_8_out, In[2]);
  and and_9 (and_9_out, In[2], not_9_out);
  not not_9 (not_9_out, In[1]);
  and and_10 (and_10_out, not_10_out, In[0]);
  not not_10 (not_10_out, In[1]);
  and and_11 (and_11_out, In[1], not_11_out);
  not not_11 (not_11_out, In[0]);
  or or_4 (C1, In[3], In[2]);
  or or_5 (C2, and_8_out, and_9_out);
  or or_6 (C3, and_10_out, and_11_out);
  Multiplexer #(.Selector_Bits(2), .Bits(4)) multiplexer_1 (
    .sel(Selector), .in_0({E0, E1, E2, E3}), .in_1({In[3], C1, C2, C3}), .in_2({_20, _21, _22, In[0]}),
    .in_3({_60, _61, _62, In[0]}), .out(Output));
  and and_12 (and_12_out, In[2], In[1]);
  and and_13 (and_13_out, In[2], In[0]);
  and and_14 (and_14_out, In[2], In[1]);
  and and_15 (and_15_out, In[2], not_12_out);
  not not_12 (not_12_out, In[0]);
  and and_16 (and_16_out, not_13_out, In[1]);
  not not_13 (not_13_out, In[2]);
  and and_17 (and_17_out, In[2], not_14_out, In[0]);
  not not_14 (not_14_out, In[1]);
  or or_7 (_20, In[3], and_12_out, and_13_out);
  or or_8 (_21, In[3], and_14_out, and_15_out);
  or or_9 (_22, In[3], and_16_out, and_17_out);
  and and_18 (and_18_out, In[2], In[0]);
  and and_19 (and_19_out, In[1], In[0]);
  and and_20 (and_20_out, In[2], In[1]);
  and and_21 (and_21_out, In[2], not_15_out);
  not not_15 (not_15_out, In[0]);
  and and_22 (and_22_out, not_16_out, not_17_out, In[0]);
  not not_16 (not_16_out, In[2]);
  not not_17 (not_17_out, In[1]);
  and and_23 (and_23_out, In[1], not_18_out);
  not not_18 (not_18_out, In[0]);
  and and_24 (and_24_out, In[2], not_19_out, In[0]);
  not not_19 (not_19_out, In[1]);
  or or_10 (_60, In[3], and_18_out, and_19_out);
  or or_11 (_61, and_20_out, and_21_out, and_22_out);
  or or_12 (_62, In[3], and_23_out, and_24_out);

  // Other names for the same wires on the sheet: _23 = In[0]; _63 = In[0]; D = In[0]; C = In[1]; B = In[2]; A = In[3];
  //   C0 = In[3]; S1 = Selector[0]; S0 = Selector[1]
endmodule
