// Digital circuit 03_04.dig as structural Verilog
module _03_04 (
  input  [6:0] In,
  output [6:0] Output
);

  wire E1, E2, E3, E4, E5, E6, E7, not_1_out, not_2_out, not_3_out, not_4_out, not_5_out, not_6_out,
       not_7_out, not_8_out, not_9_out, S1, S2, S3;

  not not_1 (not_1_out, S3);
  not not_2 (not_2_out, S2);
  not not_3 (not_3_out, S3);
  not not_4 (not_4_out, S1);
  xor xor_1 (S1, In[6], In[4], In[2], In[0]);
  xor xor_2 (S2, In[5], In[4], In[1], In[0]);
  xor xor_3 (S3, In[3], In[2], In[1], In[0]);
  and and_1 (E1, not_1_out, not_2_out, S1);
  and and_2 (E2, not_3_out, S2, not_4_out);
  xor xor_4 (Output[6], In[6], E1);
  xor xor_5 (Output[5], In[5], E2);
  xor xor_6 (Output[4], In[4], E3);
  xor xor_7 (Output[3], In[3], E4);
  xor xor_8 (Output[2], In[2], E5);
  xor xor_9 (Output[1], In[1], E6);
  xor xor_10 (Output[0], In[0], E7);
  not not_5 (not_5_out, S3);
  not not_6 (not_6_out, S2);
  not not_7 (not_7_out, S1);
  and and_3 (E3, not_5_out, S2, S1);
  and and_4 (E4, S3, not_6_out, not_7_out);
  and and_5 (E5, S3, not_8_out, S1);
  not not_8 (not_8_out, S2);
  and and_6 (E6, S3, S2, not_9_out);
  not not_9 (not_9_out, S1);
  and and_7 (E7, S3, S2, S1);

  // Other names for the same wires on the sheet: I7 = In[0]; I6 = In[1]; I5 = In[2]; I4 = In[3]; I3 = In[4];
  //   I2 = In[5]; I1 = In[6]; O1 = Output[6]; O2 = Output[5]; O3 = Output[4]; O4 = Output[3]; O5 = Output[2];
  //   O6 = Output[1]; O7 = Output[0]
endmodule
