// Digital circuit 01.dig as structural Verilog
module _01 (
  input  reset,
  input  clk,
  output A,
  output B,
  output C
);

  wire and_1_out, and_2_out, and_3_out, and_4_out, and_5_out, or_1_out, or_2_out;

  and and_1 (and_1_out, ~reset, A, ~B, C);  // And
  and and_2 (and_2_out, ~reset, ~A, B, C);  // And
  and and_3 (and_3_out, ~reset, A, ~B, C);  // And
  and and_4 (and_4_out, ~reset, ~A, ~C);  // And
  or or_1 (or_1_out, and_1_out, and_2_out);
  or or_2 (or_2_out, and_3_out, and_4_out);
  and and_5 (and_5_out, ~reset, ~A, B);  // And
  D_FF d_ff_1 (.D(or_1_out), .C(clk), .Q(A));  // open: nQ
  D_FF d_ff_2 (.D(or_2_out), .C(clk), .Q(B));  // open: nQ
  D_FF d_ff_3 (.D(and_5_out), .C(clk), .Q(C));  // open: nQ
endmodule
