// Digital circuit 02.dig as structural Verilog
module _02 (
  input  reset,
  input  X,
  input  Y,
  input  Z,
  input  load,
  input  clock,
  output A,
  output B,
  output C
);

  wire and_1_out, and_2_out, and_3_out, and_4_out, and_5_out, and_6_out, and_7_out, and_8_out, and_9_out,
       and_10_out, or_1_out, or_2_out, or_3_out;

  and and_1 (and_1_out, ~load, ~reset, A, B, ~C);  // And
  and and_2 (and_2_out, ~load, ~reset, ~A, C);  // And
  and and_3 (and_3_out, ~load, ~reset, A, ~B, C);  // And
  and and_4 (and_4_out, ~load, ~reset, A, ~B, C);  // And
  and and_5 (and_5_out, ~load, ~reset, ~C);  // And
  and and_6 (and_6_out, ~load, ~reset, A, ~B, C);  // And
  and and_7 (and_7_out, ~load, ~reset, B);  // And
  or or_1 (or_1_out, and_1_out, and_2_out, and_3_out, and_8_out);
  or or_2 (or_2_out, and_4_out, and_9_out, and_5_out);
  or or_3 (or_3_out, and_6_out, and_10_out, and_7_out);
  D_FF d_ff_1 (.D(or_1_out), .C(clock), .Q(A));  // open: nQ
  D_FF d_ff_2 (.D(or_2_out), .C(clock), .Q(B));  // open: nQ
  D_FF d_ff_3 (.D(or_3_out), .C(clock), .Q(C));  // open: nQ
  and and_8 (and_8_out, load, ~reset, X);  // And
  and and_9 (and_9_out, load, ~reset, Y);  // And
  and and_10 (and_10_out, load, ~reset, Z);  // And
endmodule

/* Test case T06:
X Y Z reset load clock A B C
0 0 0 1 0 0 x x x
0 0 0 1 0 1 0 0 0
1 1 0 0 1 0 0 0 0
1 1 0 0 1 1 1 1 0
0 0 0 0 0 0 1 1 0
0 0 0 0 0 1 1 1 1
0 0 0 0 0 0 1 1 1
0 0 0 0 0 1 0 0 1
0 0 0 0 0 0 0 0 1
0 0 0 0 0 1 1 0 0
0 0 0 0 0 0 1 0 0
0 0 0 0 0 1 0 1 0
0 0 0 0 0 0 0 1 0
0 0 0 0 0 1 0 1 1
0 0 0 0 0 0 0 1 1
0 0 0 0 0 1 1 0 1
0 0 0 0 0 0 1 0 1
0 0 0 0 0 1 1 1 1
0 0 0 0 0 0 1 1 1
0 0 0 0 0 1 0 0 1
0 0 0 0 0 0 0 0 1
*/
