// Digital circuit 03.dig as structural Verilog
module _03 (
  input  reset,
  input  [1:0] Coin,
  input  clock,
  output Open,
  output [3:0] Change
);

  wire and_1_out, and_2_out, and_3_out, and_4_out, and_5_out, and_6_out, and_7_out, and_8_out, and_9_out,
       and_10_out, and_11_out, and_12_out, and_13_out, Current0, Current1, Next0, Next1;

  D_FF #(.Bits(2)) d_ff_1 (.D({Next1, Next0}), .C(clock), .Q({Current1, Current0}));  // open: nQ
  and and_1 (and_1_out, ~Coin[1], Coin[0], ~reset, ~Current1, Current0);  // And
  and and_2 (and_2_out, Coin[1], ~Coin[0], ~reset, ~Current1, ~Current0);  // And
  and and_3 (and_3_out, ~Coin[1], Coin[0], ~reset, ~Current1, ~Current0);  // And
  and and_4 (and_4_out, Coin[1], ~Coin[0], ~reset, ~Current1, ~Current0);  // And
  and and_5 (and_5_out, Coin[1], ~Coin[0], ~reset, Current0);  // And
  and and_6 (and_6_out, Coin[1], ~Coin[0], ~reset, Current1);  // And
  and and_7 (and_7_out, Coin[1], Coin[0], ~reset, ~Current1);  // And
  and and_8 (and_8_out, Coin[0], ~reset, Current1);  // And
  and and_9 (and_9_out, Coin[1], ~Coin[0], ~reset, Current1, Current0);  // And
  and and_10 (and_10_out, Coin[1], Coin[0], ~reset, ~Current1, Current0);  // And
  and and_11 (and_11_out, Coin[0], ~reset, Current1, Current0);  // And
  and and_12 (and_12_out, Coin[1], ~Coin[0], ~reset, Current0);  // And
  and and_13 (and_13_out, Coin[1], ~Coin[0], ~reset, Current1);  // And
  or or_1 (Next1, and_1_out, and_2_out);
  or or_2 (Next0, and_3_out, and_4_out);
  or or_3 (Open, and_5_out, and_6_out, and_7_out, and_8_out);
  and and_14 (Change[3], Coin[1], Coin[0], ~reset, Current1);  // And
  and and_15 (Change[2], Coin[1], Coin[0], ~reset, ~Current1);  // And
  or or_4 (Change[1], and_9_out, and_10_out);
  or or_5 (Change[0], and_11_out, and_12_out, and_13_out);
endmodule

/* Test case T14:
reset Coin clock Open Change
1 0 0 x x
1 0 1 x x
1 0 0 0 0
1 0 1 x x
1 0 0 0 0
1 0 1 x x
1 0 0 0 0
1 0 1 x x
0 0 0 0 0
0 0 1 x x
0 0 0 0 0
0 0 1 x x
0 0 0 0 0
0 0 1 x x
0 0 0 0 0
0 0 1 x x
0 0 0 0 0
0 0 1 x x
0 0 0 0 0
0 0 1 x x
0 1 0 0 0
0 1 1 x x
0 1 0 0 0
0 1 1 x x
0 2 1 x x
0 0 0 0 0
0 0 1 x x
0 0 0 0 0
0 0 1 x x
0 0 0 0 0
0 0 1 x x
0 0 0 0 0
0 0 1 x x
1 0 0 0 0
1 0 1 x x
1 0 0 0 0
1 0 1 x x
0 0 0 0 0
0 0 1 x x
0 0 0 0 0
0 0 1 x x
0 2 0 0 0
0 2 1 x x
0 3 0 1 9
0 3 1 x x
0 0 0 0 0
0 0 1 x x
*/

/* Test case T12:
reset Coin clock Open Change
1 0 0 x x
1 0 1 x x
0 1 0 0 0
0 1 1 x x
1 0 0 0 0
1 0 1 x x
0 0 0 0 0
0 0 1 x x
0 1 0 0 0
0 1 1 x x
0 1 0 0 0
0 1 1 x x
1 0 0 0 0
1 0 1 x x
0 0 0 0 0
0 0 1 x x
0 2 0 0 0
0 2 1 x x
1 0 0 0 0
1 0 1 x x
0 0 0 0 0
0 0 1 x x
0 1 0 0 0
0 1 1 x x
0 1 0 0 0
0 1 1 x x
0 1 0 1 0
0 1 1 x x
0 0 0 0 0
0 0 1 x x
0 2 0 0 0
0 2 1 x x
0 0 0 0 0
0 0 1 x x
1 0 0 0 0
1 0 1 x x
0 3 0 1 4
0 3 1 x x
0 0 0 0 0
0 0 1 x x
*/

/* Test case T10:
reset Coin clock Open Change
1 0 0 x x
1 0 1 x x
0 0 0 0 0
0 0 1 x x
0 0 0 0 0
0 0 1 x x
0 1 0 0 0
0 1 1 x x
0 0 0 0 0
0 0 1 x x
0 0 0 0 0
0 0 1 x x
0 1 0 0 0
0 1 1 x x
0 0 0 0 0
0 0 1 x x
0 0 0 0 0
0 0 1 x x
0 0 0 0 0
0 0 1 x x
0 2 1 x x
0 0 0 0 0
0 0 1 x x
0 0 0 0 0
0 0 1 x x
0 2 0 0 0
0 2 1 x x
0 0 0 0 0
0 0 1 x x
0 0 0 0 0
0 0 1 x x
0 3 1 x x
0 0 0 0 0
0 0 1 x x
0 1 0 0 0
0 1 1 x x
0 0 0 0 0
0 0 1 x x
0 2 1 x x
0 0 0 0 0
0 0 1 x x
0 0 0 0 0
0 0 1 x x
*/

/* Test case T09:
reset Coin clock Open Change
1 0 0 x x
1 0 1 x x
0 1 0 0 0
0 1 1 x x
0 1 0 0 0
0 1 1 x x
0 3 0 1 8
0 3 1 x x
0 0 0 0 0
0 0 1 x x
0 0 0 0 0
0 0 1 x x
*/

/* Test case T07:
reset Coin clock Open Change
1 0 0 x x
1 0 1 x x
0 1 0 0 0
0 1 1 x x
0 1 0 0 0
0 1 1 x x
0 1 0 1 0
0 1 1 x x
0 0 0 0 0
0 0 1 x x
0 0 0 0 0
0 0 1 x x
*/

/* Test case T05:
reset Coin clock Open Change
1 0 0 x x
1 0 1 x x
0 1 0 0 0
0 1 1 x x
0 2 0 1 1
0 2 1 x x
0 0 0 0 0
0 0 1 x x
0 0 0 0 0
0 0 1 x x
*/

/* Test case T02:
reset Coin clock Open Change
1 0 0 x x
1 0 1 x x
0 2 0 0 0
0 2 1 x x
0 1 0 1 1
0 1 1 x x
0 0 0 0 0
0 0 1 x x
0 0 0 0 0
0 0 1 x x
*/

/* Test case T01:
reset Coin clock Open Change
1 0 0 x x
1 0 1 x x
0 3 0 1 4
0 3 1 x x
0 0 0 0 0
0 0 1 x x
0 0 0 0 0
0 0 1 x x
*/
