// Digital circuit DigLo69_MiniCpu.dig as structural Verilog
// Single-file Mini CPU: Opcode / Data / ALU / Memory-Stack / Control-Special. All original logic inlined, no custom dependencies.
module DigLo69_MiniCpu (
  input  [7:0] M,
  input  [7:0] N,
  input  [13:0] progIn,
  input  reset,
  input  progLoad,
  input  start,
  input  result,
  input  clk,
  output valid,
  output done,
  output [7:0] \output 
);

  wire accA___GCD_result, accA___memory, accA_is_prime, and_4_out, and_5_out, and_9_out, and_10_out,
       and_11_out, and_12_out, and_13_out, and_15_out, and_19_out, and_25_out, and_26_out, and_27_out,
       and_29_out, and_30_out, and_31_out, and_33_out, and_34_out, and_35_out, and_36_out, and_37_out,
       and_38_out, and_39_out, and_40_out, and_41_out, and_42_out, and_46_out, and_48_out, and_49_out,
       and_50_out, and_52_out, clearing_rRAM, cmp_a_eq_b, cmp_a_lt_b, comparator_1_eq, comparator_2_eq,
       comparator_4_gt, comparator_5_lt, comparator_6_gt, comparator_7_gt, comparator_8_eq, comparator_9_gt,
       comparator_10_eq, comparator_11_gt, comparator_12_eq, comparator_13_gt, comparator_14_eq,
       comparator_15_gt, comparator_16_eq, comparator_17_eq, comparator_19_gt, comparator_20_gt,
       comparator_21_gt, CPU_may_step, CPU_writes_rRAM, data_op_A_eq_B, data_op_A_eq_C, data_op_A_eq_D,
       data_op_A_eq_SP, data_op_B_eq_A, data_op_C_eq_A, data_op_C_eq_M, data_op_D_eq_A, data_op_D_eq_N,
       data_op_LDB, decoder_1_out_0, decoder_1_out_1, decoder_1_out_2, decoder_4_out_1, do_CMP, do_EXECUTE,
       do_FETCH__load_IR, do_PRIME, execute_Data_group, execute_Memory_group, fib_busy, FIB_done, fib_k_zero,
       FIB_or_SSUM_done, fib_regs_enable, FIB_writes_rRAM, flag_eq, flag_gr, flag_ls, gcd_busy, gcd_continue,
       GCD_done, gcd_stop_cond, gcd_x_eq_y, gcd_x_lt_y, gcd_x_zero, is_accA___pRAM, is_CMP, is_DJNZ, is_FIB,
       is_FIB_or_SSUM, is_GCD, is_isPrime, is_JEQ, is_JGR, is_JLS, is_JMP, is_JMP_or_CALL_or_RET, is_SSUM,
       is_STOP, multiplexer_14_out, multiplexer_34_out, multiplexer_57_out, multiplexer_71_out,
       multiplexer_75_out, multiplexer_76_out, multiplexer_77_out, multiplexer_79_out, multiplexer_81_out,
       multiplexer_86_out, multiplexer_88_out, no_reset_start_load, not_2_out, not_5_out, not_7_out,
       not_9_out, not_10_out, not_11_out, not_12_out, not_13_out, not_reset, op_is_CALL, op_is_LD, op_is_LDC,
       op_is_POP, op_is_POP_or_RET, op_is_PUSH, op_is_PUSH_or_CALL, op_is_PUSH_or_POP, op_is_RET, op_is_ST,
       op_is_STC, or_7_out, or_8_out, or_9_out, or_10_out, or_11_out, or_12_out, or_13_out, or_14_out,
       or_16_out, or_17_out, or_19_out, or_20_out, or_21_out, or_22_out, or_23_out, or_24_out, or_25_out,
       or_26_out, or_27_out, or_28_out, or_29_out, or_31_out, or_32_out, or_33_out, or_34_out, or_35_out,
       or_36_out, or_38_out, or_39_out, or_41_out, or_42_out, or_43_out, or_44_out, or_45_out, or_46_out,
       or_48_out, or_49_out, or_50_out, or_51_out, prime_a_lt_2, reset_edge, reset_or_start,
       reset_start_load, reset_was_low, result_asked_or_sending, result_last_byte, rRAM_ready__not_clearing,
       sending_result, ssum_mode, ssum_mode_d, ssum_mode_t1, ssum_mode_t2, ssum_reading, ssum_rem_nonzero,
       ssum_rem_zero, ssum_step, start_FIB, start_GCD, start_SSUM, state__eq__EXECUTE, state__eq__FETCH,
       state__eq__FIB_compute, state__eq__FIB_write_high, state__eq__FIB_write_low, state__eq__GCD_loop,
       write_accA, write_regD__DJNZ;
  wire [2:0] multiplexer_12_out, multiplexer_16_out, multiplexer_18_out, multiplexer_19_out,
       multiplexer_21_out, multiplexer_23_out, multiplexer_25_out, multiplexer_26_out, state;
  wire [3:0] alu_b_low_nibble;
  wire [4:0] fib_k, multiplexer_60_out, multiplexer_69_out, multiplexer_74_out, sub_7_s;
  wire [5:0] opcode;
  wire [7:0] accA, accB, add_1_s, add_2_s, add_3_s, add_6_s, add_9_s, alu_a_mod_b, ALU_result, and_8_out,
       and_18_out, barrelshifter_1_out, barrelshifter_2_out, barrelshifter_3_out, barrelshifter_4_out,
       clear_address, clear_count, CPU_rRAM_address, div_1_r, div_2_r, div_3_q, div_4_r, div_5_r, div_6_r,
       div_7_r, FIB_address, FIB_byte, fib_f0_high_byte, FIB_hi_addr, FIB_lo_addr, GCD_result, gcd_x, gcd_y,
       jump_target, memory_read_value, mul_1_mul, multiplexer_5_out, multiplexer_7_out, multiplexer_8_out,
       multiplexer_9_out, multiplexer_10_out, multiplexer_11_out, multiplexer_15_out, multiplexer_17_out,
       multiplexer_20_out, multiplexer_22_out, multiplexer_31_out, multiplexer_32_out, multiplexer_33_out,
       multiplexer_39_out, multiplexer_40_out, multiplexer_41_out, multiplexer_42_out, multiplexer_43_out,
       multiplexer_51_out, multiplexer_52_out, multiplexer_54_out, multiplexer_55_out, multiplexer_56_out,
       multiplexer_59_out, multiplexer_61_out, multiplexer_62_out, multiplexer_63_out, multiplexer_64_out,
       multiplexer_65_out, multiplexer_66_out, multiplexer_68_out, multiplexer_72_out, multiplexer_73_out,
       multiplexer_80_out, multiplexer_83_out, multiplexer_85_out, multiplexer_87_out, multiplexer_90_out,
       multiplexer_92_out, neg_SP, new_accA_value, not_6_out, operand, or_5_out, PC, PC__plus__1,
       pram_load_addr, regC, regD, regD___1, result_address, result_count, rRAM_access_address,
       rRAM_write_data__CPU, SP, sp_dec, special_result, ssum_ptr, ssum_ptr__plus__1, ssum_ptr_d, ssum_ptr_n,
       ssum_rem, ssum_rem___1, ssum_rem_d, ssum_rem_n, sub_1_s, sub_2_s, sub_3_s, xor_1_out;
  wire [7:4] alu_operand_b;
  wire [13:0] instruction__pRAM_out;
  wire [15:0] add_8_s, FIB_f0, fib_f1, multiplexer_53_out, multiplexer_58_out, multiplexer_67_out,
       multiplexer_78_out, multiplexer_82_out, multiplexer_84_out, ssum_acc, ssum_acc__plus__d, ssum_acc_d,
       ssum_acc_n;

  Comparator #(.Signed("false"), .Bits(8)) comparator_1 (
    .a(accA), .b(8'h2), .eq(comparator_1_eq), .lt(prime_a_lt_2));  // open: gt
  or or_1 (op_is_PUSH_or_CALL, op_is_PUSH, op_is_CALL);
  or or_2 (op_is_POP_or_RET, op_is_POP, op_is_RET);
  or or_3 (is_JMP_or_CALL_or_RET, is_JMP, op_is_CALL, op_is_RET);
  Multiplexer #(.Bits(8)) multiplexer_1 (.sel(op_is_CALL), .in_0(accA), .in_1(PC__plus__1), .out(rRAM_write_data__CPU));
  Multiplexer #(.Bits(8)) multiplexer_2 (.sel(op_is_RET), .in_0(operand), .in_1(\output ), .out(jump_target));
  not not_1 (not_reset, reset);
  D_FF #(.Bits(1)) reset_last_clock (.D(reset), .C(clk), .nQ(reset_was_low));  // open: Q
  Multiplexer #(.Bits(8)) multiplexer_3 (.sel(gcd_x_zero), .in_0(gcd_x), .in_1(gcd_y), .out(GCD_result));
  Comparator #(.Signed("false"), .Bits(8)) comparator_2 (
    .a(gcd_y), .b({8{1'b0}}), .eq(comparator_2_eq));  // open: gt, lt
  Comparator #(.Signed("false"), .Bits(8)) comparator_3 (.a(gcd_x), .b({8{1'b0}}), .eq(gcd_x_zero));  // open: gt, lt
  Comparator #(.Signed("false"), .Bits(8)) comparator_4 (
    .a(gcd_x), .b(gcd_y), .gt(comparator_4_gt), .eq(gcd_x_eq_y), .lt(gcd_x_lt_y));
  Div #(.Bits(8)) div_1 (.a(accA), .b(8'h2), .r(div_1_r));  // open: q
  Div #(.Bits(8)) div_2 (.a(accA), .b(8'h3), .r(div_2_r));  // open: q
  Add #(.Bits(8)) add_1 (.a(pram_load_addr), .b(8'h1), .c_i(1'b0), .s(add_1_s));  // open: c_o
  not not_2 (not_2_out, clearing_rRAM);
  Comparator #(.Signed("false"), .Bits(8)) comparator_5 (
    .a(clear_count), .b(8'h10), .lt(comparator_5_lt));  // open: gt, eq
  Multiplexer #(.Bits(8)) multiplexer_4 (.sel(reset_edge), .in_0(clear_count), .in_1({8{1'b0}}), .out(clear_address));
  and and_1 (reset_edge, reset, reset_was_low);
  and and_2 (do_FETCH__load_IR, state__eq__FETCH, CPU_may_step);
  not not_3 (no_reset_start_load, reset_start_load);
  and and_3 (do_EXECUTE, state__eq__EXECUTE, CPU_may_step);
  and and_4 (and_4_out, gcd_busy, gcd_stop_cond);
  not not_4 (gcd_continue, gcd_stop_cond);
  Multiplexer #(.Bits(8)) multiplexer_5 (
    .sel(accA___memory), .in_0(ALU_result), .in_1(memory_read_value), .out(multiplexer_5_out));
  Register #(.Bits(14)) IR__instruction_register (
    .D(instruction__pRAM_out), .C(clk), .en(do_FETCH__load_IR), .Q({opcode, operand}));
  Div #(.Bits(8)) div_3 (.a(accA), .b({alu_operand_b, alu_b_low_nibble}), .q(div_3_q), .r(alu_a_mod_b));
  and and_5 (and_5_out, execute_Memory_group, is_accA___pRAM);
  and and_6 (rRAM_ready__not_clearing, not_reset, not_2_out);
  Comparator #(.Signed("false"), .Bits(8)) comparator_6 (
    .a(div_1_r), .b({8{1'b0}}), .gt(comparator_6_gt));  // open: eq, lt
  Comparator #(.Signed("false"), .Bits(8)) comparator_7 (
    .a(div_2_r), .b({8{1'b0}}), .gt(comparator_7_gt));  // open: eq, lt
  Comparator #(.Signed("false"), .Bits(8)) comparator_8 (.a(accA), .b(8'h3), .eq(comparator_8_eq));  // open: gt, lt
  Div #(.Bits(8)) div_4 (.a(accA), .b(8'h5), .r(div_4_r));  // open: q
  Div #(.Bits(8)) div_5 (.a(accA), .b(8'h7), .r(div_5_r));  // open: q
  Add #(.Bits(8)) add_2 (.a(accA), .b({alu_operand_b, alu_b_low_nibble}), .c_i(1'b0), .s(add_2_s));  // open: c_o
  Sub #(.Bits(8)) sub_1 (.a(accA), .b({alu_operand_b, alu_b_low_nibble}), .c_i(1'b0), .s(sub_1_s));  // open: c_o
  and and_7 (CPU_may_step, no_reset_start_load, rRAM_ready__not_clearing);
  or or_4 (gcd_stop_cond, gcd_x_eq_y, gcd_x_zero, comparator_2_eq);
  Multiplexer #(.Bits(8)) multiplexer_6 (
    .sel(accA___GCD_result), .in_0(multiplexer_5_out), .in_1(GCD_result), .out(new_accA_value));
  Mul #(.Bits(4)) mul_1 (.a(accA[3:0]), .b(alu_b_low_nibble), .mul(mul_1_mul));
  assign and_8_out = accA & {alu_operand_b, alu_b_low_nibble};  // And and_8, 8 bits wide
  assign or_5_out = accA | {alu_operand_b, alu_b_low_nibble};  // Or or_5, 8 bits wide
  assign xor_1_out = accA ^ {alu_operand_b, alu_b_low_nibble};  // XOr xor_1, 8 bits wide
  Multiplexer #(.Bits(8)) multiplexer_7 (
    .sel(progLoad), .in_0(pram_load_addr), .in_1(add_1_s), .out(multiplexer_7_out));
  or or_6 (clearing_rRAM, reset_edge, comparator_5_lt);
  or or_7 (or_7_out, GCD_done, and_4_out);
  not not_5 (not_5_out, prime_a_lt_2);
  or or_8 (or_8_out, comparator_6_gt, comparator_1_eq);
  or or_9 (or_9_out, comparator_7_gt, comparator_8_eq);
  Comparator #(.Signed("false"), .Bits(8)) comparator_9 (
    .a(div_4_r), .b({8{1'b0}}), .gt(comparator_9_gt));  // open: eq, lt
  Comparator #(.Signed("false"), .Bits(8)) comparator_10 (.a(accA), .b(8'h5), .eq(comparator_10_eq));  // open: gt, lt
  Comparator #(.Signed("false"), .Bits(8)) comparator_11 (
    .a(div_5_r), .b({8{1'b0}}), .gt(comparator_11_gt));  // open: eq, lt
  Comparator #(.Signed("false"), .Bits(8)) comparator_12 (.a(accA), .b(8'h7), .eq(comparator_12_eq));  // open: gt, lt
  Div #(.Bits(8)) div_6 (.a(accA), .b(8'hb), .r(div_6_r));  // open: q
  Seven_Seg_Hex seven_seg_hex_1 (.d(\output [7:4]), .dp(1'b0));
  Seven_Seg_Hex seven_seg_hex_2 (.d(\output [3:0]), .dp(1'b0));
  assign not_6_out = ~accA;  // Not not_6, 8 bits wide
  BarrelShifter #(.Bits(8)) barrelshifter_1 (.in(accA), .shift(alu_b_low_nibble), .out(barrelshifter_1_out));
  BarrelShifter #(.Bits(8), .direction("right")) barrelshifter_2 (
    .in(accA), .shift(alu_b_low_nibble), .out(barrelshifter_2_out));
  Multiplexer #(.Bits(8)) multiplexer_8 (.sel(and_5_out), .in_0(PC), .in_1(operand), .out(multiplexer_8_out));
  not not_7 (not_7_out, start_GCD);
  Sub #(.Bits(8)) sub_2 (.a(gcd_x), .b(gcd_y), .c_i(1'b0), .s(sub_2_s));  // open: c_o
  Div #(.Bits(8)) div_7 (.a(accA), .b(8'hd), .r(div_7_r));  // open: q
  BarrelShifter #(.Bits(8), .barrelShifterMode("rotate")) barrelshifter_3 (
    .in(accA), .shift(alu_b_low_nibble), .out(barrelshifter_3_out));
  BarrelShifter #(.Bits(8), .barrelShifterMode("rotate"), .direction("right")) barrelshifter_4 (
    .in(accA), .shift(alu_b_low_nibble), .out(barrelshifter_4_out));
  Multiplexer #(.Bits(8)) multiplexer_9 (
    .sel(reset), .in_0(multiplexer_7_out), .in_1({8{1'b0}}), .out(multiplexer_9_out));
  and and_9 (and_9_out, or_7_out, not_7_out);
  and and_10 (and_10_out, gcd_busy, comparator_4_gt, gcd_continue);
  and and_11 (and_11_out, not_5_out, or_8_out, or_9_out);
  or or_10 (or_10_out, comparator_9_gt, comparator_10_eq);
  or or_11 (or_11_out, comparator_11_gt, comparator_12_eq);
  Comparator #(.Signed("false"), .Bits(8)) comparator_13 (
    .a(div_6_r), .b({8{1'b0}}), .gt(comparator_13_gt));  // open: eq, lt
  Comparator #(.Signed("false"), .Bits(8)) comparator_14 (.a(accA), .b(8'hb), .eq(comparator_14_eq));  // open: gt, lt
  Decoder #(.Selector_Bits(2)) decoder_1 (
    .sel(opcode[5:4]), .out_0(decoder_1_out_0), .out_1(decoder_1_out_1), .out_2(decoder_1_out_2));  // open: out_3
  Comparator #(.Signed("false"), .Bits(8)) comparator_15 (
    .a(div_7_r), .b({8{1'b0}}), .gt(comparator_15_gt));  // open: eq, lt
  Comparator #(.Signed("false"), .Bits(8)) comparator_16 (.a(accA), .b(8'hd), .eq(comparator_16_eq));  // open: gt, lt
  Multiplexer #(.Bits(8)) multiplexer_10 (.sel(start_GCD), .in_0(sub_2_s), .in_1(accA), .out(multiplexer_10_out));
  and and_12 (and_12_out, and_11_out, or_10_out, or_11_out);
  or or_12 (or_12_out, comparator_13_gt, comparator_14_eq);
  or or_13 (or_13_out, comparator_15_gt, comparator_16_eq);
  Multiplexer #(.Bits(8)) multiplexer_11 (
    .sel(progLoad), .in_0(multiplexer_8_out), .in_1(pram_load_addr), .out(multiplexer_11_out));
  and and_13 (and_13_out, progLoad, not_reset);
  D_FF #(.Bits(8)) program_load_address (.D(multiplexer_9_out), .C(clk), .Q(pram_load_addr));  // open: nQ
  or or_14 (or_14_out, start_GCD, and_10_out);
  and and_14 (execute_Memory_group, do_EXECUTE, decoder_1_out_1);
  and and_15 (and_15_out, do_EXECUTE, decoder_1_out_2);
  and and_16 (execute_Data_group, do_EXECUTE, decoder_1_out_0);
  Multiplexer #(.Bits(3)) multiplexer_12 (.sel(is_GCD), .in_0(3'b001), .in_1(3'b011), .out(multiplexer_12_out));
  and and_17 (accA_is_prime, and_12_out, or_12_out, or_13_out);
  Multiplexer #(.Bits(8), .Selector_Bits(4)) multiplexer_13 (
    .sel(opcode[3:0]), .in_0(add_2_s), .in_1(sub_1_s), .in_2(mul_1_mul), .in_3({8{1'b0}}), .in_4(div_3_q),
    .in_5(alu_a_mod_b), .in_6({8{1'b0}}), .in_7({8{1'b0}}), .in_8(and_8_out), .in_9(or_5_out),
    .in_10(xor_1_out), .in_11(not_6_out), .in_12(barrelshifter_1_out), .in_13(barrelshifter_2_out),
    .in_14(barrelshifter_3_out), .in_15(barrelshifter_4_out), .out(ALU_result));
  Add #(.Bits(8)) add_3 (.a(clear_count), .b(8'h1), .c_i(1'b0), .s(add_3_s));  // open: c_o
  Multiplexer #(.Bits(1)) multiplexer_14 (
    .sel(reset_start_load), .in_0(and_9_out), .in_1(1'b0), .out(multiplexer_14_out));
  Multiplexer #(.Bits(8)) multiplexer_15 (
    .sel(or_14_out), .in_0(gcd_x), .in_1(multiplexer_10_out), .out(multiplexer_15_out));
  or or_15 (write_accA, and_15_out, accA___memory, accA___GCD_result);
  RAMDualPort #(.AddrBits(8), .Bits(14)) pRAM (
    .A(multiplexer_11_out), .Din(progIn), .str(and_13_out), .C(clk), .ld(1'b1), .D(instruction__pRAM_out));
  Multiplexer #(.Bits(3)) multiplexer_16 (
    .sel(is_FIB_or_SSUM), .in_0(multiplexer_12_out), .in_1(3'b100), .out(multiplexer_16_out));
  D_FF #(.Bits(1)) u_GCD_done (.D(multiplexer_14_out), .C(clk), .Q(GCD_done));  // open: nQ
  Multiplexer #(.Bits(8)) multiplexer_17 (.sel(reset_edge), .in_0(add_3_s), .in_1(8'h1), .out(multiplexer_17_out));
  Multiplexer #(.Bits(3)) multiplexer_18 (
    .sel(is_STOP), .in_0(multiplexer_16_out), .in_1(3'b111), .out(multiplexer_18_out));
  Multiplexer #(.Bits(3)) multiplexer_19 (.sel(GCD_done), .in_0(3'b011), .in_1(3'b001), .out(multiplexer_19_out));
  Multiplexer #(.Bits(8)) multiplexer_20 (
    .sel(reset_start_load), .in_0(multiplexer_15_out), .in_1({8{1'b0}}), .out(multiplexer_20_out));
  assign and_18_out = accB & 8'h7;  // And and_18, 8 bits wide
  Multiplexer #(.Bits(3)) multiplexer_21 (
    .sel(FIB_or_SSUM_done), .in_0(3'b100), .in_1(3'b101), .out(multiplexer_21_out));
  D_FF #(.Bits(8)) u_GCD_x (.D(multiplexer_20_out), .C(clk), .Q(gcd_x));  // open: nQ
  Comparator #(.Signed("false"), .Bits(2)) comparator_17 (
    .a(opcode[3:2]), .b(2'b11), .eq(comparator_17_eq));  // open: gt, lt
  Multiplexer #(.Bits(8)) multiplexer_22 (
    .sel(clearing_rRAM), .in_0(clear_count), .in_1(multiplexer_17_out), .out(multiplexer_22_out));
  Multiplexer #(.Bits(3), .Selector_Bits(3)) multiplexer_23 (
    .sel(state), .in_0(3'b000), .in_1(3'b010), .in_2(multiplexer_18_out), .in_3(multiplexer_19_out),
    .in_4(multiplexer_21_out), .in_5(3'b110), .in_6(3'b001), .in_7(3'b111), .out(multiplexer_23_out));
  Decoder #(.Selector_Bits(6)) decoder_2 (
    .sel(opcode), .out_16(op_is_LD), .out_17(op_is_ST), .out_18(is_accA___pRAM), .out_20(op_is_LDC),
    .out_21(op_is_STC), .out_24(op_is_PUSH), .out_25(op_is_POP), .out_28(op_is_CALL), .out_29(op_is_RET),
    .out_48(is_JMP), .out_49(is_JEQ), .out_50(is_JGR), .out_51(is_JLS), .out_52(is_DJNZ), .out_56(is_CMP),
    .out_57(is_isPrime), .out_60(is_GCD), .out_61(is_FIB), .out_62(is_SSUM), .out_63(is_STOP));  // open: out_0, out_1, out_2, out_3, out_4, out_5, out_6, out_7, out_8, out_9, out_10, out_11, out_12, out_13, out_14, out_15, out_19, out_22, out_23, out_26, out_27, out_30, out_31, out_32, out_33, out_34, out_35, out_36, out_37, out_38, out_39, out_40, out_41, out_42, out_43, out_44, out_45, out_46, out_47, out_53, out_54, out_55, out_58, out_59
  Multiplexer #(.Bits(8)) multiplexer_24 (
    .sel(comparator_17_eq), .in_0(accB), .in_1(and_18_out), .out({alu_operand_b, alu_b_low_nibble}));
  and and_19 (and_19_out, start, rRAM_ready__not_clearing);
  and and_20 (start_GCD, do_EXECUTE, is_GCD);
  and and_21 (start_FIB, do_EXECUTE, is_FIB);
  D_FF #(.Bits(8)) clear_counter (.D(multiplexer_22_out), .C(clk), .Q(clear_count));  // open: nQ
  Multiplexer #(.Bits(3)) multiplexer_25 (
    .sel(and_19_out), .in_0(multiplexer_23_out), .in_1(3'b001), .out(multiplexer_25_out));
  or or_16 (or_16_out, reset, progLoad);
  or or_17 (or_17_out, reset, progLoad, sending_result);
  Multiplexer #(.Bits(3)) multiplexer_26 (
    .sel(or_16_out), .in_0(multiplexer_25_out), .in_1(3'b000), .out(multiplexer_26_out));
  Sub #(.Bits(8)) sub_3 (.a(gcd_y), .b(gcd_x), .c_i(1'b0), .s(sub_3_s));  // open: c_o
  or or_18 (is_FIB_or_SSUM, is_FIB, is_SSUM);
  and and_22 (start_SSUM, do_EXECUTE, is_SSUM);
  Multiplexer #(.Bits(1)) multiplexer_27 (.sel(start_FIB), .in_0(ssum_mode), .in_1(1'b0), .out(ssum_mode_t1));
  Multiplexer #(.Bits(1)) multiplexer_28 (.sel(start_SSUM), .in_0(ssum_mode_t1), .in_1(1'b1), .out(ssum_mode_t2));
  Multiplexer #(.Bits(1)) multiplexer_29 (.sel(reset_start_load), .in_0(ssum_mode_t2), .in_1(1'b0), .out(ssum_mode_d));
  D_FF #(.Bits(1)) u_SSUM_mode (.D(ssum_mode_d), .C(clk), .Q(ssum_mode));  // open: nQ
  Comparator #(.Signed("false"), .Bits(8)) comparator_18 (
    .a(ssum_rem), .b({8{1'b0}}), .eq(ssum_rem_zero));  // open: gt, lt
  not not_8 (ssum_rem_nonzero, ssum_rem_zero);
  and and_23 (ssum_reading, state__eq__FIB_compute, ssum_mode);
  and and_24 (ssum_step, ssum_reading, ssum_rem_nonzero);
  Multiplexer #(.Bits(8)) multiplexer_30 (
    .sel(is_accA___pRAM), .in_0(\output ), .in_1(instruction__pRAM_out[7:0]), .out(memory_read_value));
  and and_25 (and_25_out, gcd_busy, gcd_continue);
  and and_26 (and_26_out, gcd_busy, gcd_x_lt_y, gcd_continue);
  Multiplexer #(.Bits(8)) multiplexer_31 (
    .sel(FIB_writes_rRAM), .in_0(rRAM_access_address), .in_1(FIB_address), .out(multiplexer_31_out));
  D_FF #(.Bits(3)) u_state (.D(multiplexer_26_out), .C(clk), .Q(state));  // open: nQ
  Decoder #(.Selector_Bits(3)) decoder_3 (
    .sel(state), .out_1(state__eq__FETCH), .out_2(state__eq__EXECUTE), .out_3(state__eq__GCD_loop),
    .out_4(state__eq__FIB_compute), .out_5(state__eq__FIB_write_high), .out_6(state__eq__FIB_write_low),
    .out_7(valid));  // open: out_0
  Multiplexer #(.Bits(8)) multiplexer_32 (.sel(start_GCD), .in_0(sub_3_s), .in_1(accB), .out(multiplexer_32_out));
  or or_19 (or_19_out, or_17_out, result);
  or or_20 (or_20_out, start_GCD, and_25_out);
  or or_21 (or_21_out, start_GCD, and_26_out);
  or or_22 (or_22_out, CPU_writes_rRAM, FIB_writes_rRAM);
  not not_9 (not_9_out, or_19_out);
  Multiplexer #(.Bits(8)) multiplexer_33 (
    .sel(or_21_out), .in_0(gcd_y), .in_1(multiplexer_32_out), .out(multiplexer_33_out));
  and and_27 (and_27_out, or_22_out, not_9_out);
  Multiplexer #(.Bits(1)) multiplexer_34 (
    .sel(reset_start_load), .in_0(or_20_out), .in_1(1'b0), .out(multiplexer_34_out));
  Sub #(.Bits(8)) sub_4 (.a({8{1'b0}}), .b(SP), .c_i(1'b0), .s(neg_SP));  // open: c_o
  Sub #(.Bits(8)) sub_5 (.a(ssum_rem), .b(8'h1), .c_i(1'b0), .s(ssum_rem___1));  // open: c_o
  Multiplexer #(.Bits(8)) multiplexer_35 (.sel(ssum_step), .in_0(ssum_rem), .in_1(ssum_rem___1), .out(ssum_rem_n));
  Multiplexer #(.Bits(8)) multiplexer_36 (.sel(start_SSUM), .in_0(ssum_rem_n), .in_1(neg_SP), .out(ssum_rem_d));
  D_FF #(.Bits(8)) SSUM_remaining (.D(ssum_rem_d), .C(clk), .Q(ssum_rem));  // open: nQ
  Add #(.Bits(8)) add_4 (.a(ssum_ptr), .b(8'h1), .c_i(1'b0), .s(ssum_ptr__plus__1));  // open: c_o
  Multiplexer #(.Bits(8)) multiplexer_37 (.sel(ssum_step), .in_0(ssum_ptr), .in_1(ssum_ptr__plus__1), .out(ssum_ptr_n));
  Multiplexer #(.Bits(8)) multiplexer_38 (.sel(start_SSUM), .in_0(ssum_ptr_n), .in_1(SP), .out(ssum_ptr_d));
  D_FF #(.Bits(8)) SSUM_pointer (.D(ssum_ptr_d), .C(clk), .Q(ssum_ptr));  // open: nQ
  Multiplexer #(.Bits(8)) multiplexer_39 (
    .sel(result_asked_or_sending), .in_0(multiplexer_31_out), .in_1(result_address), .out(multiplexer_39_out));
  Multiplexer #(.Bits(8)) multiplexer_40 (
    .sel(FIB_writes_rRAM), .in_0(rRAM_write_data__CPU), .in_1(FIB_byte), .out(multiplexer_40_out));
  Sub #(.Bits(8)) sub_6 (.a(regD), .b(8'h1), .c_i(1'b0), .s(regD___1));  // open: c_o
  and and_28 (write_regD__DJNZ, do_EXECUTE, is_DJNZ);
  D_FF #(.Bits(1)) u_GCD_busy (.D(multiplexer_34_out), .C(clk), .Q(gcd_busy));  // open: nQ
  Multiplexer #(.Bits(8)) multiplexer_41 (
    .sel(reset_start_load), .in_0(multiplexer_33_out), .in_1({8{1'b0}}), .out(multiplexer_41_out));
  Multiplexer #(.Bits(8)) multiplexer_42 (
    .sel(clearing_rRAM), .in_0(multiplexer_39_out), .in_1(clear_address), .out(multiplexer_42_out));
  Multiplexer #(.Bits(8)) multiplexer_43 (
    .sel(clearing_rRAM), .in_0(multiplexer_40_out), .in_1({8{1'b0}}), .out(multiplexer_43_out));
  or or_23 (or_23_out, clearing_rRAM, and_27_out);
  or or_24 (or_24_out, data_op_C_eq_A, data_op_C_eq_M);
  or or_25 (or_25_out, data_op_D_eq_A, data_op_D_eq_N);
  or or_26 (or_26_out, data_op_LDB, data_op_B_eq_A);
  D_FF #(.Bits(8)) u_GCD_y (.D(multiplexer_41_out), .C(clk), .Q(gcd_y));  // open: nQ
  RAMDualPort #(.AddrBits(8), .Bits(8)) rRAM (
    .A(multiplexer_42_out), .Din(multiplexer_43_out), .str(or_23_out), .C(clk), .ld(1'b1), .D(\output ));
  Add #(.Bits(16)) add_5 (.a(ssum_acc), .b({{8{1'b0}}, \output }), .c_i(1'b0), .s(ssum_acc__plus__d));  // open: c_o
  Multiplexer #(.Bits(16)) multiplexer_44 (
    .sel(ssum_step), .in_0(ssum_acc), .in_1(ssum_acc__plus__d), .out(ssum_acc_n));
  Multiplexer #(.Bits(16)) multiplexer_45 (.sel(start_SSUM), .in_0(ssum_acc_n), .in_1({16{1'b0}}), .out(ssum_acc_d));
  D_FF #(.Bits(16)) SSUM_accumulator (.D(ssum_acc_d), .C(clk), .Q(ssum_acc));  // open: nQ
  Multiplexer #(.Bits(8)) multiplexer_46 (
    .sel(ssum_reading), .in_0(CPU_rRAM_address), .in_1(ssum_ptr), .out(rRAM_access_address));
  Multiplexer #(.Bits(1)) multiplexer_47 (
    .sel(ssum_mode), .in_0(FIB_done), .in_1(ssum_rem_zero), .out(FIB_or_SSUM_done));
  Multiplexer #(.Bits(8)) multiplexer_48 (.sel(ssum_mode), .in_0(8'ha), .in_1(8'hc), .out(FIB_hi_addr));
  Multiplexer #(.Bits(8)) multiplexer_49 (.sel(ssum_mode), .in_0(8'hb), .in_1(8'hd), .out(FIB_lo_addr));
  Multiplexer #(.Bits(16)) multiplexer_50 (
    .sel(ssum_mode), .in_0(FIB_f0), .in_1(ssum_acc), .out({fib_f0_high_byte, special_result}));
  or or_27 (or_27_out, is_GCD, is_FIB_or_SSUM, is_STOP);
  and and_29 (and_29_out, or_24_out, execute_Data_group);
  and and_30 (and_30_out, or_25_out, execute_Data_group);
  and and_31 (and_31_out, or_26_out, execute_Data_group);
  not not_10 (not_10_out, or_27_out);
  and and_32 (accA___GCD_result, state__eq__GCD_loop, GCD_done, CPU_may_step);
  Multiplexer #(.Bits(8)) multiplexer_51 (.sel(data_op_C_eq_M), .in_0(accA), .in_1(M), .out(multiplexer_51_out));
  Multiplexer #(.Bits(8)) multiplexer_52 (.sel(data_op_B_eq_A), .in_0(operand), .in_1(accA), .out(multiplexer_52_out));
  and and_33 (and_33_out, is_JEQ, flag_eq);
  Multiplexer #(.Bits(16)) multiplexer_53 (.sel(start_FIB), .in_0(fib_f1), .in_1({16{1'b0}}), .out(multiplexer_53_out));
  Sub #(.Bits(5)) sub_7 (.a(fib_k), .b(5'b00001), .c_i(1'b0), .s(sub_7_s));  // open: c_o
  Comparator #(.Signed("false"), .Bits(5)) comparator_19 (
    .a(fib_k), .b({5{1'b0}}), .gt(comparator_19_gt), .eq(fib_k_zero));  // open: lt
  Multiplexer #(.Bits(8)) multiplexer_54 (.sel(data_op_D_eq_N), .in_0(accA), .in_1(N), .out(multiplexer_54_out));
  and and_34 (and_34_out, is_JGR, flag_gr);
  and and_35 (and_35_out, fib_busy, fib_k_zero);
  Multiplexer #(.Bits(8)) multiplexer_55 (
    .sel(reset), .in_0(multiplexer_51_out), .in_1({8{1'b0}}), .out(multiplexer_55_out));
  or or_28 (or_28_out, and_29_out, reset);
  Multiplexer #(.Bits(8)) multiplexer_56 (
    .sel(reset), .in_0(multiplexer_52_out), .in_1({8{1'b0}}), .out(multiplexer_56_out));
  or or_29 (or_29_out, and_31_out, reset);
  Comparator #(.Signed("false"), .Bits(8)) comparator_20 (
    .a(regD___1), .b({8{1'b0}}), .gt(comparator_20_gt));  // open: eq, lt
  Multiplexer #(.Bits(1)) multiplexer_57 (
    .sel(reset_start_load), .in_0(fib_regs_enable), .in_1(1'b0), .out(multiplexer_57_out));
  Add #(.Bits(8)) add_6 (.a(SP), .b(8'h1), .c_i(1'b0), .s(add_6_s));  // open: c_o
  Sub #(.Bits(8)) sub_8 (.a(SP), .b(8'h1), .c_i(1'b0), .s(sp_dec));  // open: c_o
  or or_30 (reset_or_start, reset, start);
  or or_31 (or_31_out, is_JMP_or_CALL_or_RET, and_33_out, and_34_out);
  and and_36 (and_36_out, is_JLS, flag_ls);
  and and_37 (and_37_out, do_EXECUTE, not_10_out);
  and and_38 (and_38_out, fib_busy, comparator_19_gt);
  Register #(.Bits(8)) u_regC (.D(multiplexer_55_out), .C(clk), .en(or_28_out), .Q(regC));
  or or_32 (or_32_out, and_30_out, write_regD__DJNZ);
  Register #(.Bits(8)) u_accB (.D(multiplexer_56_out), .C(clk), .en(or_29_out), .Q(accB));
  or or_33 (or_33_out, op_is_LDC, op_is_STC);
  Add #(.Bits(8)) add_7 (.a(PC), .b(8'h1), .c_i(1'b0), .s(PC__plus__1));  // open: c_o
  and and_39 (and_39_out, is_DJNZ, comparator_20_gt);
  Multiplexer #(.Bits(16)) multiplexer_58 (
    .sel(fib_regs_enable), .in_0(FIB_f0), .in_1(multiplexer_53_out), .out(multiplexer_58_out));
  or or_34 (or_34_out, FIB_done, and_35_out);
  D_FF #(.Bits(1)) u_FIB_busy (.D(multiplexer_57_out), .C(clk), .Q(fib_busy));  // open: nQ
  Multiplexer #(.Bits(8)) multiplexer_59 (
    .sel(write_regD__DJNZ), .in_0(multiplexer_54_out), .in_1(regD___1), .out(multiplexer_59_out));
  Multiplexer #(.Bits(5)) multiplexer_60 (.sel(start_FIB), .in_0(sub_7_s), .in_1(accA[4:0]), .out(multiplexer_60_out));
  not not_11 (not_11_out, start_FIB);
  Multiplexer #(.Bits(8)) multiplexer_61 (
    .sel(op_is_PUSH_or_CALL), .in_0(add_6_s), .in_1(sp_dec), .out(multiplexer_61_out));
  or or_35 (or_35_out, or_31_out, and_36_out, and_39_out);
  and and_40 (and_40_out, state__eq__FIB_write_low, CPU_may_step);
  and and_41 (and_41_out, or_34_out, not_11_out);
  Multiplexer #(.Bits(8)) multiplexer_62 (
    .sel(reset), .in_0(multiplexer_59_out), .in_1({8{1'b0}}), .out(multiplexer_62_out));
  or or_36 (or_36_out, or_32_out, reset);
  Multiplexer #(.Bits(8)) multiplexer_63 (.sel(or_33_out), .in_0(operand), .in_1(regC), .out(multiplexer_63_out));
  Multiplexer #(.Bits(8)) multiplexer_64 (.sel(op_is_PUSH_or_CALL), .in_0(SP), .in_1(sp_dec), .out(multiplexer_64_out));
  and and_42 (and_42_out, execute_Memory_group, op_is_PUSH_or_POP);
  Multiplexer #(.Bits(8)) multiplexer_65 (
    .sel(or_35_out), .in_0(PC__plus__1), .in_1(jump_target), .out(multiplexer_65_out));
  or or_37 (fib_regs_enable, start_FIB, and_38_out);
  Multiplexer #(.Bits(8)) multiplexer_66 (
    .sel(and_42_out), .in_0(SP), .in_1(multiplexer_61_out), .out(multiplexer_66_out));
  or or_38 (or_38_out, and_37_out, accA___GCD_result, and_40_out);
  Multiplexer #(.Bits(16)) multiplexer_67 (
    .sel(reset_start_load), .in_0(multiplexer_58_out), .in_1({16{1'b0}}), .out(multiplexer_67_out));
  Register #(.Bits(8)) u_regD (.D(multiplexer_62_out), .C(clk), .en(or_36_out), .Q(regD));
  Multiplexer #(.Bits(8)) multiplexer_68 (
    .sel(or_38_out), .in_0(PC), .in_1(multiplexer_65_out), .out(multiplexer_68_out));
  Multiplexer #(.Bits(5)) multiplexer_69 (
    .sel(fib_regs_enable), .in_0(fib_k), .in_1(multiplexer_60_out), .out(multiplexer_69_out));
  Multiplexer #(.Bits(8)) multiplexer_70 (
    .sel(op_is_PUSH_or_POP), .in_0(multiplexer_63_out), .in_1(multiplexer_64_out), .out(CPU_rRAM_address));
  D_FF #(.Bits(16)) u_FIB_f0 (.D(multiplexer_67_out), .C(clk), .Q(FIB_f0));  // open: nQ
  Multiplexer #(.Bits(1)) multiplexer_71 (
    .sel(reset_start_load), .in_0(and_41_out), .in_1(1'b0), .out(multiplexer_71_out));
  Multiplexer #(.Bits(8)) multiplexer_72 (
    .sel(reset_or_start), .in_0(multiplexer_66_out), .in_1({8{1'b0}}), .out(multiplexer_72_out));
  Multiplexer #(.Bits(8)) multiplexer_73 (
    .sel(reset_or_start), .in_0(multiplexer_68_out), .in_1({8{1'b0}}), .out(multiplexer_73_out));
  Multiplexer #(.Bits(5)) multiplexer_74 (
    .sel(reset_start_load), .in_0(multiplexer_69_out), .in_1({5{1'b0}}), .out(multiplexer_74_out));
  D_FF #(.Bits(1)) u_FIB_done (.D(multiplexer_71_out), .C(clk), .Q(FIB_done));  // open: nQ
  D_FF #(.Bits(8)) u_SP (.D(multiplexer_72_out), .C(clk), .Q(SP));  // open: nQ
  Decoder #(.Selector_Bits(4)) decoder_4 (
    .sel(opcode[3:0]), .out_1(decoder_4_out_1), .out_2(data_op_LDB), .out_4(data_op_A_eq_B),
    .out_5(data_op_B_eq_A), .out_6(data_op_C_eq_A), .out_7(data_op_D_eq_A), .out_8(data_op_A_eq_C),
    .out_9(data_op_A_eq_D), .out_10(data_op_A_eq_SP), .out_12(data_op_C_eq_M), .out_13(data_op_D_eq_N));  // open: out_0, out_3, out_11, out_14, out_15
  D_FF #(.Bits(8)) u_PC (.D(multiplexer_73_out), .C(clk), .Q(PC));  // open: nQ
  D_FF #(.Bits(5)) FIB_counter (.D(multiplexer_74_out), .C(clk), .Q(fib_k));  // open: nQ
  or or_39 (or_39_out, op_is_ST, op_is_STC, op_is_PUSH_or_CALL);
  or or_40 (op_is_PUSH_or_POP, op_is_PUSH_or_CALL, op_is_POP_or_RET);
  or or_41 (or_41_out, op_is_LD, is_accA___pRAM, op_is_LDC);
  Add #(.Bits(16)) add_8 (.a(FIB_f0), .b(fib_f1), .c_i(1'b0), .s(add_8_s));  // open: c_o
  and and_43 (do_PRIME, do_EXECUTE, is_isPrime);
  and and_44 (do_CMP, do_EXECUTE, is_CMP);
  Multiplexer #(.Bits(1)) multiplexer_75 (.sel(do_CMP), .in_0(flag_ls), .in_1(cmp_a_lt_b), .out(multiplexer_75_out));
  or or_42 (or_42_out, decoder_4_out_1, data_op_A_eq_B, data_op_A_eq_C, data_op_A_eq_D, data_op_A_eq_SP);
  Multiplexer #(.Bits(1)) multiplexer_76 (
    .sel(do_PRIME), .in_0(cmp_a_eq_b), .in_1(accA_is_prime), .out(multiplexer_76_out));
  or or_43 (or_43_out, or_41_out, op_is_POP);
  or or_44 (or_44_out, do_CMP, do_PRIME);
  Multiplexer #(.Bits(1)) multiplexer_77 (
    .sel(reset), .in_0(multiplexer_75_out), .in_1(1'b0), .out(multiplexer_77_out));
  Multiplexer #(.Bits(16)) multiplexer_78 (.sel(start_FIB), .in_0(add_8_s), .in_1(16'h1), .out(multiplexer_78_out));
  and and_45 (CPU_writes_rRAM, execute_Memory_group, or_39_out);
  Multiplexer #(.Bits(1)) multiplexer_79 (
    .sel(or_44_out), .in_0(flag_eq), .in_1(multiplexer_76_out), .out(multiplexer_79_out));
  D_FF #(.Bits(1)) u_flag_ls (.D(multiplexer_77_out), .C(clk), .Q(flag_ls));  // open: nQ
  Multiplexer #(.Selector_Bits(4), .Bits(8)) multiplexer_80 (
    .sel(opcode[3:0]), .in_0(accA), .in_1(operand), .in_2(accA), .in_3(accA), .in_4(accB), .in_5(accA),
    .in_6(accA), .in_7(accA), .in_8(regC), .in_9(regD), .in_10(SP), .in_11(accA), .in_12(accA), .in_13(accA),
    .in_14(accA), .in_15(accA), .out(multiplexer_80_out));
  and and_46 (and_46_out, or_42_out, execute_Data_group);
  Multiplexer #(.Bits(1)) multiplexer_81 (
    .sel(reset), .in_0(multiplexer_79_out), .in_1(1'b0), .out(multiplexer_81_out));
  Multiplexer #(.Bits(16)) multiplexer_82 (
    .sel(fib_regs_enable), .in_0(fib_f1), .in_1(multiplexer_78_out), .out(multiplexer_82_out));
  and and_47 (accA___memory, execute_Memory_group, or_43_out);
  D_FF #(.Bits(1)) u_flag_eq (.D(multiplexer_81_out), .C(clk), .Q(flag_eq));  // open: nQ
  or or_45 (or_45_out, and_46_out, write_accA);
  Multiplexer #(.Bits(8)) multiplexer_83 (
    .sel(write_accA), .in_0(multiplexer_80_out), .in_1(new_accA_value), .out(multiplexer_83_out));
  Multiplexer #(.Bits(16)) multiplexer_84 (
    .sel(reset_start_load), .in_0(multiplexer_82_out), .in_1({16{1'b0}}), .out(multiplexer_84_out));
  Multiplexer #(.Bits(8)) multiplexer_85 (
    .sel(reset), .in_0(multiplexer_83_out), .in_1({8{1'b0}}), .out(multiplexer_85_out));
  or or_46 (or_46_out, or_45_out, reset);
  Comparator #(.Signed("true"), .Bits(8)) comparator_21 (
    .a(accA), .b(accB), .gt(comparator_21_gt), .eq(cmp_a_eq_b), .lt(cmp_a_lt_b));
  D_FF #(.Bits(16)) u_FIB_f1 (.D(multiplexer_84_out), .C(clk), .Q(fib_f1));  // open: nQ
  Register #(.Bits(8)) u_accA (.D(multiplexer_85_out), .C(clk), .en(or_46_out), .Q(accA));
  or or_47 (reset_start_load, reset, start, progLoad);
  and and_48 (and_48_out, sending_result, result_last_byte);
  Comparator #(.Signed("false"), .Bits(8)) comparator_22 (
    .a(result_count), .b(8'hf), .eq(result_last_byte));  // open: gt, lt
  not not_12 (not_12_out, result_last_byte);
  Add #(.Bits(8)) add_9 (.a(result_count), .b(8'h1), .c_i(1'b0), .s(add_9_s));  // open: c_o
  Multiplexer #(.Bits(1)) multiplexer_86 (
    .sel(do_CMP), .in_0(flag_gr), .in_1(comparator_21_gt), .out(multiplexer_86_out));
  and and_49 (and_49_out, sending_result, not_12_out);
  or or_48 (or_48_out, reset_start_load, result);
  Multiplexer #(.Bits(8)) multiplexer_87 (.sel(result), .in_0(add_9_s), .in_1({8{1'b0}}), .out(multiplexer_87_out));
  Multiplexer #(.Bits(1)) multiplexer_88 (
    .sel(reset), .in_0(multiplexer_86_out), .in_1(1'b0), .out(multiplexer_88_out));
  or or_49 (or_49_out, done, and_48_out);
  not not_13 (not_13_out, or_48_out);
  or or_50 (or_50_out, state__eq__FIB_write_high, state__eq__FIB_write_low);
  Multiplexer #(.Bits(8)) multiplexer_89 (
    .sel(state__eq__FIB_write_low), .in_0(FIB_hi_addr), .in_1(FIB_lo_addr), .out(FIB_address));
  and and_50 (and_50_out, or_49_out, not_13_out);
  or or_51 (or_51_out, result, and_49_out);
  D_FF #(.Bits(1)) u_flag_gr (.D(multiplexer_88_out), .C(clk), .Q(flag_gr));  // open: nQ
  D_FF #(.Bits(1)) u_done (.D(and_50_out), .C(clk), .Q(done));  // open: nQ
  Multiplexer #(.Bits(8)) multiplexer_90 (
    .sel(result_asked_or_sending), .in_0(result_count), .in_1(multiplexer_87_out), .out(multiplexer_90_out));
  and and_51 (FIB_writes_rRAM, or_50_out, CPU_may_step);
  Multiplexer #(.Bits(8)) multiplexer_91 (
    .sel(state__eq__FIB_write_low), .in_0(fib_f0_high_byte), .in_1(special_result), .out(FIB_byte));
  and and_52 (and_52_out, or_51_out, no_reset_start_load);
  Multiplexer #(.Bits(8)) multiplexer_92 (
    .sel(reset), .in_0(multiplexer_90_out), .in_1({8{1'b0}}), .out(multiplexer_92_out));
  D_FF #(.Bits(8)) result_counter (.D(multiplexer_92_out), .C(clk), .Q(result_count));  // open: nQ
  D_FF #(.Bits(1)) u_sending_result (.D(and_52_out), .C(clk), .Q(sending_result));  // open: nQ
  or or_52 (result_asked_or_sending, result, sending_result);
  Multiplexer #(.Bits(8)) multiplexer_93 (.sel(result), .in_0(result_count), .in_1({8{1'b0}}), .out(result_address));

  // Other names for the same wires on the sheet: opcode_low_nibble[3:0] = opcode[3:0];
  //   FIB_n__eq__accA_4_0[4:0] = accA[4:0]; alu_operand_b[3:0] = alu_b_low_nibble;
  //   pRAM_data__7_0[7:0] = instruction__pRAM_out[7:0]; rRAM_data_out[7:0] = \output ;
  //   rRAM_data_out_16[7:0] = \output ; special_result[15:8] = fib_f0_high_byte

  // Notes on the sheet:
  //   01 CORE - IR / DECODE / I-O / REGISTERS
  //   OPCODE: IR / decoder / I-O / writeback
  //   02 ALU - ARITHMETIC / LOGIC / SHIFT
  //   ALU: arith/logic/shift + B[2:0] adapter
  //   03 MEMORY - PROGRAM RAM / RESULT RAM / STACK
  //   Program RAM: load pointer, fetch, LDP
  //   Reset: 16-clock rRAM clear, pRAM kept
  //   04 CONTROL - FSM / NEXT STATE / PC / FLAGS
  //   FSM decode: separate FETCH/EXECUTE edges
  //   05 SPECIAL OPS - GCD / FIB / PRIME
  //   GCD: load -> compare/subtract -> done
  //   PRIME: trial division by 2,3,5,7,11,13
  //   06 SECRET OPS - CALL / RET / SSUM
  //   CALL/RET: share PUSH/POP path, PC+1 to stack, stack to PC
  //   Next state: 2-cycle path + wait/write
  //   Special: private regs, keeps accB/flags
  //   Decoders: opcode (6-bit) + FSM state (3-bit)
  //   rRAM address/data/write arbitration
  //   SSUM: temp ptr/rem/acc regs, reuses FIB write states (addr 0x0C/0x0D)
  //   PC and DJNZ: dec D before branch test
  //   DATA: registers / MUX / decoder / reset
  //   FIB: load f0=0 f1=1 k=n, iterate, done
  //   Stack: descending SP, PUSH SP-1, POP SP
  //   Flags: signed CMP; PRIME sets only eq
  //   Result stream: bytes 0..15 then done
  //   FIB commit: hi byte 0x0A, lo byte 0x0B
  //   6933029821 เกียรติศักดิ์ แสนบุรี
  //   6933272921 สิรวิชญ์ รูปงาม
  //   6933018921 กันตินันท์ สวัสดิ์วงษ์
endmodule

/* Test case 01_P01T01:
M N progIn reset progLoad start result clk valid done output
0 0 0 0 0 0 0 0 x x x
0 0 0 0 0 0 0 1 x x x
0 0 0 1 0 0 0 0 x x x
0 0 0 1 0 0 0 1 0 0 x
0 0 0 0 0 0 0 0 0 x x
0 0 0 0 0 0 0 1 0 x x
0 0 0 0 0 0 0 0 0 x x
0 0 0 0 0 0 0 1 0 x x
0 0 0 0 0 0 0 0 0 x x
0 0 0 0 0 0 0 1 0 x x
0 0 0 0 0 0 0 0 0 x x
0 0 0 0 0 0 0 1 0 x x
0 0 0 0 0 0 0 0 0 x x
0 0 0 0 0 0 0 1 0 x x
0 0 0 0 0 0 0 0 0 x x
0 0 0 0 0 0 0 1 0 x x
0 0 0 0 0 0 0 0 0 x x
0 0 0 0 0 0 0 1 0 x x
0 0 0 0 0 0 0 0 0 x x
0 0 0 0 0 0 0 1 0 x x
0 0 0 0 0 0 0 0 0 x x
0 0 0 0 0 0 0 1 0 x x
0 0 0 0 0 0 0 0 0 x x
0 0 0 0 0 0 0 1 0 x x
0 0 0 0 0 0 0 0 0 x x
0 0 0 0 0 0 0 1 0 x x
0 0 0 0 0 0 0 0 0 x x
0 0 0 0 0 0 0 1 0 x x
0 0 0 0 0 0 0 0 0 x x
0 0 0 0 0 0 0 1 0 x x
0 0 0 0 0 0 0 0 0 x x
0 0 0 0 0 0 0 1 0 x x
0 0 0 0 0 0 0 0 0 x x
0 0 0 0 0 0 0 1 0 x x
0 0 0 0 0 0 0 0 0 x x
0 0 0 0 0 0 0 1 0 x x
0 0 0 0 0 0 0 0 0 x x
0 0 0 0 0 0 0 1 0 x x
0 0 0 0 0 0 0 0 0 x x
0 0 0 0 0 0 0 1 0 x x
0 0 0 0 0 0 0 0 0 x x
0 0 0 0 0 0 0 1 0 x x
0 0 0 0 0 0 0 0 0 x x
0 0 0 0 0 0 0 1 0 x x
0 0 271 0 1 0 0 0 0 x x
0 0 271 0 1 0 0 1 0 x x
0 0 565 0 1 0 0 0 0 x x
0 0 565 0 1 0 0 1 0 x x
0 0 8192 0 1 0 0 0 0 x x
0 0 8192 0 1 0 0 1 0 x x
0 0 4355 0 1 0 0 0 0 x x
0 0 4355 0 1 0 0 1 0 x x
0 0 16128 0 1 0 0 0 0 x x
0 0 16128 0 1 0 0 1 0 x x
0 0 0 0 0 1 0 0 x x x
0 0 0 0 0 1 0 1 x 0 x
0 0 0 0 0 0 0 0 x 0 x
0 0 0 0 0 0 0 1 x 0 x
0 0 0 0 0 0 0 0 x 0 x
0 0 0 0 0 0 0 1 x 0 x
0 0 0 0 0 0 0 0 x 0 x
0 0 0 0 0 0 0 1 x 0 x
0 0 0 0 0 0 0 0 x 0 x
0 0 0 0 0 0 0 1 x 0 x
0 0 0 0 0 0 0 0 x 0 x
0 0 0 0 0 0 0 1 x 0 x
0 0 0 0 0 0 0 0 x 0 x
0 0 0 0 0 0 0 1 x 0 x
0 0 0 0 0 0 0 0 x 0 x
0 0 0 0 0 0 0 1 x 0 x
0 0 0 0 0 0 0 0 x 0 x
0 0 0 0 0 0 0 1 x 0 x
0 0 0 0 0 0 0 0 x 0 x
0 0 0 0 0 0 0 1 x 0 x
0 0 0 0 0 0 0 0 x 0 x
0 0 0 0 0 0 0 1 x 0 x
0 0 0 0 0 0 0 0 x 0 x
0 0 0 0 0 0 0 1 x 0 x
0 0 0 0 0 0 0 0 x 0 x
0 0 0 0 0 0 0 1 x 0 x
0 0 0 0 0 0 0 0 x 0 x
0 0 0 0 0 0 0 1 x 0 x
0 0 0 0 0 0 0 0 x 0 x
0 0 0 0 0 0 0 1 x 0 x
0 0 0 0 0 0 0 0 x 0 x
0 0 0 0 0 0 0 1 x 0 x
0 0 0 0 0 0 0 0 x 0 x
0 0 0 0 0 0 0 1 x 0 x
0 0 0 0 0 0 0 0 x 0 x
0 0 0 0 0 0 0 1 x 0 x
0 0 0 0 0 0 0 0 x 0 x
0 0 0 0 0 0 0 1 x 0 x
0 0 0 0 0 0 0 0 x 0 x
0 0 0 0 0 0 0 1 x 0 x
0 0 0 0 0 0 0 0 x 0 x
0 0 0 0 0 0 0 1 x 0 x
0 0 0 0 0 0 0 0 x 0 x
0 0 0 0 0 0 0 1 x 0 x
0 0 0 0 0 0 0 0 x 0 x
0 0 0 0 0 0 0 1 x 0 x
0 0 0 0 0 0 0 0 x 0 x
0 0 0 0 0 0 0 1 x 0 x
0 0 0 0 0 0 0 0 x 0 x
0 0 0 0 0 0 0 1 1 0 x
0 0 0 0 0 0 1 0 1 x x
0 0 0 0 0 0 1 1 1 0 0
0 0 0 0 0 0 0 0 1 0 0
0 0 0 0 0 0 0 1 1 0 0
0 0 0 0 0 0 0 0 1 0 0
0 0 0 0 0 0 0 1 1 0 0
0 0 0 0 0 0 0 0 1 0 0
0 0 0 0 0 0 0 1 1 0 68
0 0 0 0 0 0 0 0 1 0 68
0 0 0 0 0 0 0 1 1 0 0
0 0 0 0 0 0 0 0 1 0 0
0 0 0 0 0 0 0 1 1 0 0
0 0 0 0 0 0 0 0 1 0 0
0 0 0 0 0 0 0 1 1 0 0
0 0 0 0 0 0 0 0 1 0 0
0 0 0 0 0 0 0 1 1 0 0
0 0 0 0 0 0 0 0 1 0 0
0 0 0 0 0 0 0 1 1 0 0
0 0 0 0 0 0 0 0 1 0 0
0 0 0 0 0 0 0 1 1 0 0
0 0 0 0 0 0 0 0 1 0 0
0 0 0 0 0 0 0 1 1 0 0
0 0 0 0 0 0 0 0 1 0 0
0 0 0 0 0 0 0 1 1 0 0
0 0 0 0 0 0 0 0 1 0 0
0 0 0 0 0 0 0 1 1 0 0
0 0 0 0 0 0 0 0 1 0 0
0 0 0 0 0 0 0 1 1 0 0
0 0 0 0 0 0 0 0 1 0 0
0 0 0 0 0 0 0 1 1 0 0
0 0 0 0 0 0 0 0 1 0 0
0 0 0 0 0 0 0 1 1 0 0
0 0 0 0 0 0 0 0 1 x 0
0 0 0 0 0 0 0 1 1 1 x
0 0 0 0 0 0 0 0 1 1 x
0 0 0 0 0 0 0 1 1 1 x
*/

/* Test case 20_P07T02:
M N progIn reset progLoad start result clk valid done output
0 0 0 0 0 0 0 C x x x
0 0 0 1 0 0 0 C 0 0 x
repeat(20) 0 0 0 0 0 0 0 C 0 x x
0 0 320 0 1 0 0 C 0 x x
0 0 1536 0 1 0 0 C 0 x x
0 0 264 0 1 0 0 C 0 x x
0 0 1792 0 1 0 0 C 0 x x
0 0 259 0 1 0 0 C 0 x x
0 0 5376 0 1 0 0 C 0 x x
0 0 517 0 1 0 0 C 0 x x
0 0 8192 0 1 0 0 C 0 x x
0 0 1280 0 1 0 0 C 0 x x
0 0 2048 0 1 0 0 C 0 x x
0 0 513 0 1 0 0 C 0 x x
0 0 8192 0 1 0 0 C 0 x x
0 0 1536 0 1 0 0 C 0 x x
0 0 1024 0 1 0 0 C 0 x x
0 0 13317 0 1 0 0 C 0 x x
0 0 327 0 1 0 0 C 0 x x
0 0 1536 0 1 0 0 C 0 x x
0 0 264 0 1 0 0 C 0 x x
0 0 1792 0 1 0 0 C 0 x x
0 0 5120 0 1 0 0 C 0 x x
0 0 6144 0 1 0 0 C 0 x x
0 0 2048 0 1 0 0 C 0 x x
0 0 513 0 1 0 0 C 0 x x
0 0 8448 0 1 0 0 C 0 x x
0 0 1536 0 1 0 0 C 0 x x
0 0 13331 0 1 0 0 C 0 x x
0 0 256 0 1 0 0 C 0 x x
0 0 1536 0 1 0 0 C 0 x x
0 0 264 0 1 0 0 C 0 x x
0 0 1792 0 1 0 0 C 0 x x
0 0 6400 0 1 0 0 C 0 x x
0 0 5376 0 1 0 0 C 0 x x
0 0 2048 0 1 0 0 C 0 x x
0 0 513 0 1 0 0 C 0 x x
0 0 8192 0 1 0 0 C 0 x x
0 0 1536 0 1 0 0 C 0 x x
0 0 13342 0 1 0 0 C 0 x x
0 0 16128 0 1 0 0 C 0 x x
0 0 0 0 0 1 0 C x 0 x
repeat(827) 0 0 0 0 0 0 0 C x 0 x
0 0 0 0 0 0 0 C 1 0 x
0 0 0 0 0 0 1 C 1 0 3
repeat(7) 0 0 0 0 0 0 0 C 1 0 1
repeat(8) 0 0 0 0 0 0 0 C 1 0 0
repeat(2) 0 0 0 0 0 0 0 C 1 1 x
*/

/* Test case S01_CALLRET_example:
M N progIn reset progLoad start result clk valid done output
0 0 0 0 0 0 0 C x x x
0 0 0 1 0 0 0 C 0 0 x
repeat(20) 0 0 0 0 0 0 0 C 0 x x
0 0 261 0 1 0 0 C 0 x x
0 0 7174 0 1 0 0 C 0 x x
0 0 4352 0 1 0 0 C 0 x x
0 0 2560 0 1 0 0 C 0 x x
0 0 4353 0 1 0 0 C 0 x x
0 0 16128 0 1 0 0 C 0 x x
0 0 1280 0 1 0 0 C 0 x x
0 0 8192 0 1 0 0 C 0 x x
0 0 7424 0 1 0 0 C 0 x x
0 0 0 0 0 1 0 C x 0 x
repeat(60) 0 0 0 0 0 0 0 C x 0 x
0 0 0 0 0 0 0 C 1 0 x
0 0 0 0 0 0 1 C 1 0 10
0 0 0 0 0 0 0 C 1 0 0
0 0 0 0 0 0 0 C 1 0 0
0 0 0 0 0 0 0 C 1 0 0
0 0 0 0 0 0 0 C 1 0 0
0 0 0 0 0 0 0 C 1 0 0
0 0 0 0 0 0 0 C 1 0 0
0 0 0 0 0 0 0 C 1 0 0
0 0 0 0 0 0 0 C 1 0 0
0 0 0 0 0 0 0 C 1 0 0
0 0 0 0 0 0 0 C 1 0 0
0 0 0 0 0 0 0 C 1 0 0
0 0 0 0 0 0 0 C 1 0 0
0 0 0 0 0 0 0 C 1 0 0
0 0 0 0 0 0 0 C 1 0 0
0 0 0 0 0 0 0 C 1 0 0
repeat(2) 0 0 0 0 0 0 0 C 1 1 x
*/

/* Test case 14_P01T02:
M N progIn reset progLoad start result clk valid done output
0 0 0 0 0 0 0 C x x x
0 0 0 1 0 0 0 C 0 0 x
repeat(20) 0 0 0 0 0 0 0 C 0 x x
0 0 346 0 1 0 0 C 0 x x
0 0 4352 0 1 0 0 C 0 x x
0 0 677 0 1 0 0 C 0 x x
0 0 1024 0 1 0 0 C 0 x x
0 0 4367 0 1 0 0 C 0 x x
0 0 375 0 1 0 0 C 0 x x
0 0 4359 0 1 0 0 C 0 x x
0 0 16128 0 1 0 0 C 0 x x
0 0 0 0 0 1 0 C x 0 x
repeat(35) 0 0 0 0 0 0 0 C x 0 x
0 0 0 0 0 0 0 C 1 0 x
0 0 0 0 0 0 1 C 1 0 90
repeat(6) 0 0 0 0 0 0 0 C 1 0 0
0 0 0 0 0 0 0 C 1 0 119
repeat(7) 0 0 0 0 0 0 0 C 1 0 0
0 0 0 0 0 0 0 C 1 0 165
repeat(2) 0 0 0 0 0 0 0 C 1 1 x
0 0 0 0 0 0 1 C 1 0 90
repeat(6) 0 0 0 0 0 0 0 C 1 0 0
0 0 0 0 0 0 0 C 1 0 119
repeat(7) 0 0 0 0 0 0 0 C 1 0 0
0 0 0 0 0 0 0 C 1 0 165
repeat(2) 0 0 0 0 0 0 0 C 1 1 x
*/

/* Test case 08_P08T01:
M N progIn reset progLoad start result clk valid done output
0 0 0 0 0 0 0 0 x x x
0 0 0 0 0 0 0 1 x x x
0 0 0 1 0 0 0 0 x x x
0 0 0 1 0 0 0 1 0 0 x
0 0 0 0 0 0 0 0 0 x x
0 0 0 0 0 0 0 1 0 x x
0 0 0 0 0 0 0 0 0 x x
0 0 0 0 0 0 0 1 0 x x
0 0 0 0 0 0 0 0 0 x x
0 0 0 0 0 0 0 1 0 x x
0 0 0 0 0 0 0 0 0 x x
0 0 0 0 0 0 0 1 0 x x
0 0 0 0 0 0 0 0 0 x x
0 0 0 0 0 0 0 1 0 x x
0 0 0 0 0 0 0 0 0 x x
0 0 0 0 0 0 0 1 0 x x
0 0 0 0 0 0 0 0 0 x x
0 0 0 0 0 0 0 1 0 x x
0 0 0 0 0 0 0 0 0 x x
0 0 0 0 0 0 0 1 0 x x
0 0 0 0 0 0 0 0 0 x x
0 0 0 0 0 0 0 1 0 x x
0 0 0 0 0 0 0 0 0 x x
0 0 0 0 0 0 0 1 0 x x
0 0 0 0 0 0 0 0 0 x x
0 0 0 0 0 0 0 1 0 x x
0 0 0 0 0 0 0 0 0 x x
0 0 0 0 0 0 0 1 0 x x
0 0 0 0 0 0 0 0 0 x x
0 0 0 0 0 0 0 1 0 x x
0 0 0 0 0 0 0 0 0 x x
0 0 0 0 0 0 0 1 0 x x
0 0 0 0 0 0 0 0 0 x x
0 0 0 0 0 0 0 1 0 x x
0 0 0 0 0 0 0 0 0 x x
0 0 0 0 0 0 0 1 0 x x
0 0 0 0 0 0 0 0 0 x x
0 0 0 0 0 0 0 1 0 x x
0 0 0 0 0 0 0 0 0 x x
0 0 0 0 0 0 0 1 0 x x
0 0 0 0 0 0 0 0 0 x x
0 0 0 0 0 0 0 1 0 x x
0 0 0 0 0 0 0 0 0 x x
0 0 0 0 0 0 0 1 0 x x
0 0 356 0 1 0 0 0 0 x x
0 0 356 0 1 0 0 1 0 x x
0 0 572 0 1 0 0 0 0 x x
0 0 572 0 1 0 0 1 0 x x
0 0 8192 0 1 0 0 0 0 x x
0 0 8192 0 1 0 0 1 0 x x
0 0 4352 0 1 0 0 0 0 x x
0 0 4352 0 1 0 0 1 0 x x
0 0 266 0 1 0 0 0 0 x x
0 0 266 0 1 0 0 1 0 x x
0 0 542 0 1 0 0 0 0 x x
0 0 542 0 1 0 0 1 0 x x
0 0 8448 0 1 0 0 0 0 x x
0 0 8448 0 1 0 0 1 0 x x
0 0 4353 0 1 0 0 0 0 x x
0 0 4353 0 1 0 0 1 0 x x
0 0 311 0 1 0 0 0 0 x x
0 0 311 0 1 0 0 1 0 x x
0 0 557 0 1 0 0 0 0 x x
0 0 557 0 1 0 0 1 0 x x
0 0 8704 0 1 0 0 0 0 x x
0 0 8704 0 1 0 0 1 0 x x
0 0 4354 0 1 0 0 0 0 x x
0 0 4354 0 1 0 0 1 0 x x
0 0 456 0 1 0 0 0 0 x x
0 0 456 0 1 0 0 1 0 x x
0 0 612 0 1 0 0 0 0 x x
0 0 612 0 1 0 0 1 0 x x
0 0 8192 0 1 0 0 0 0 x x
0 0 8192 0 1 0 0 1 0 x x
0 0 4355 0 1 0 0 0 0 x x
0 0 4355 0 1 0 0 1 0 x x
0 0 16128 0 1 0 0 0 0 x x
0 0 16128 0 1 0 0 1 0 x x
0 0 0 0 0 1 0 0 x x x
0 0 0 0 0 1 0 1 x 0 x
0 0 0 0 0 0 0 0 x 0 x
0 0 0 0 0 0 0 1 x 0 x
0 0 0 0 0 0 0 0 x 0 x
0 0 0 0 0 0 0 1 x 0 x
0 0 0 0 0 0 0 0 x 0 x
0 0 0 0 0 0 0 1 x 0 x
0 0 0 0 0 0 0 0 x 0 x
0 0 0 0 0 0 0 1 x 0 x
0 0 0 0 0 0 0 0 x 0 x
0 0 0 0 0 0 0 1 x 0 x
0 0 0 0 0 0 0 0 x 0 x
0 0 0 0 0 0 0 1 x 0 x
0 0 0 0 0 0 0 0 x 0 x
0 0 0 0 0 0 0 1 x 0 x
0 0 0 0 0 0 0 0 x 0 x
0 0 0 0 0 0 0 1 x 0 x
0 0 0 0 0 0 0 0 x 0 x
0 0 0 0 0 0 0 1 x 0 x
0 0 0 0 0 0 0 0 x 0 x
0 0 0 0 0 0 0 1 x 0 x
0 0 0 0 0 0 0 0 x 0 x
0 0 0 0 0 0 0 1 x 0 x
0 0 0 0 0 0 0 0 x 0 x
0 0 0 0 0 0 0 1 x 0 x
0 0 0 0 0 0 0 0 x 0 x
0 0 0 0 0 0 0 1 x 0 x
0 0 0 0 0 0 0 0 x 0 x
0 0 0 0 0 0 0 1 x 0 x
0 0 0 0 0 0 0 0 x 0 x
0 0 0 0 0 0 0 1 x 0 x
0 0 0 0 0 0 0 0 x 0 x
0 0 0 0 0 0 0 1 x 0 x
0 0 0 0 0 0 0 0 x 0 x
0 0 0 0 0 0 0 1 x 0 x
0 0 0 0 0 0 0 0 x 0 x
0 0 0 0 0 0 0 1 x 0 x
0 0 0 0 0 0 0 0 x 0 x
0 0 0 0 0 0 0 1 x 0 x
0 0 0 0 0 0 0 0 x 0 x
0 0 0 0 0 0 0 1 x 0 x
0 0 0 0 0 0 0 0 x 0 x
0 0 0 0 0 0 0 1 x 0 x
0 0 0 0 0 0 0 0 x 0 x
0 0 0 0 0 0 0 1 x 0 x
0 0 0 0 0 0 0 0 x 0 x
0 0 0 0 0 0 0 1 x 0 x
0 0 0 0 0 0 0 0 x 0 x
0 0 0 0 0 0 0 1 x 0 x
0 0 0 0 0 0 0 0 x 0 x
0 0 0 0 0 0 0 1 x 0 x
0 0 0 0 0 0 0 0 x 0 x
0 0 0 0 0 0 0 1 x 0 x
0 0 0 0 0 0 0 0 x 0 x
0 0 0 0 0 0 0 1 x 0 x
0 0 0 0 0 0 0 0 x 0 x
0 0 0 0 0 0 0 1 x 0 x
0 0 0 0 0 0 0 0 x 0 x
0 0 0 0 0 0 0 1 x 0 x
0 0 0 0 0 0 0 0 x 0 x
0 0 0 0 0 0 0 1 x 0 x
0 0 0 0 0 0 0 0 x 0 x
0 0 0 0 0 0 0 1 x 0 x
0 0 0 0 0 0 0 0 x 0 x
0 0 0 0 0 0 0 1 x 0 x
0 0 0 0 0 0 0 0 x 0 x
0 0 0 0 0 0 0 1 x 0 x
0 0 0 0 0 0 0 0 x 0 x
0 0 0 0 0 0 0 1 x 0 x
0 0 0 0 0 0 0 0 x 0 x
0 0 0 0 0 0 0 1 x 0 x
0 0 0 0 0 0 0 0 x 0 x
0 0 0 0 0 0 0 1 x 0 x
0 0 0 0 0 0 0 0 x 0 x
0 0 0 0 0 0 0 1 x 0 x
0 0 0 0 0 0 0 0 x 0 x
0 0 0 0 0 0 0 1 x 0 x
0 0 0 0 0 0 0 0 x 0 x
0 0 0 0 0 0 0 1 x 0 x
0 0 0 0 0 0 0 0 x 0 x
0 0 0 0 0 0 0 1 x 0 x
0 0 0 0 0 0 0 0 x 0 x
0 0 0 0 0 0 0 1 x 0 x
0 0 0 0 0 0 0 0 x 0 x
0 0 0 0 0 0 0 1 x 0 x
0 0 0 0 0 0 0 0 x 0 x
0 0 0 0 0 0 0 1 x 0 x
0 0 0 0 0 0 0 0 x 0 x
0 0 0 0 0 0 0 1 x 0 x
0 0 0 0 0 0 0 0 x 0 x
0 0 0 0 0 0 0 1 x 0 x
0 0 0 0 0 0 0 0 x 0 x
0 0 0 0 0 0 0 1 x 0 x
0 0 0 0 0 0 0 0 x 0 x
0 0 0 0 0 0 0 1 x 0 x
0 0 0 0 0 0 0 0 x 0 x
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*/

/* Test case S02_CALL_nested_stack:
M N progIn reset progLoad start result clk valid done output
0 0 0 0 0 0 0 C x x x
0 0 0 1 0 0 0 C 0 0 x
repeat(20) 0 0 0 0 0 0 0 C 0 x x
0 0 259 0 1 0 0 C 0 x x
0 0 7175 0 1 0 0 C 0 x x
0 0 4352 0 1 0 0 C 0 x x
0 0 2560 0 1 0 0 C 0 x x
0 0 4353 0 1 0 0 C 0 x x
0 0 16128 0 1 0 0 C 0 x x
0 0 0 0 1 0 0 C 0 x x
0 0 6144 0 1 0 0 C 0 x x
0 0 266 0 1 0 0 C 0 x x
0 0 7182 0 1 0 0 C 0 x x
0 0 1280 0 1 0 0 C 0 x x
0 0 6400 0 1 0 0 C 0 x x
0 0 8192 0 1 0 0 C 0 x x
0 0 7424 0 1 0 0 C 0 x x
0 0 1280 0 1 0 0 C 0 x x
0 0 8192 0 1 0 0 C 0 x x
0 0 7424 0 1 0 0 C 0 x x
0 0 0 0 0 1 0 C x 0 x
repeat(120) 0 0 0 0 0 0 0 C x 0 x
0 0 0 0 0 0 0 C 1 0 x
0 0 0 0 0 0 1 C 1 0 23
0 0 0 0 0 0 0 C 1 0 0
0 0 0 0 0 0 0 C 1 0 0
0 0 0 0 0 0 0 C 1 0 0
0 0 0 0 0 0 0 C 1 0 0
0 0 0 0 0 0 0 C 1 0 0
0 0 0 0 0 0 0 C 1 0 0
0 0 0 0 0 0 0 C 1 0 0
0 0 0 0 0 0 0 C 1 0 0
0 0 0 0 0 0 0 C 1 0 0
0 0 0 0 0 0 0 C 1 0 0
0 0 0 0 0 0 0 C 1 0 0
0 0 0 0 0 0 0 C 1 0 0
0 0 0 0 0 0 0 C 1 0 0
0 0 0 0 0 0 0 C 1 0 0
0 0 0 0 0 0 0 C 1 0 0
repeat(2) 0 0 0 0 0 0 0 C 1 1 x
0 0 0 0 0 1 0 C x 0 x
repeat(120) 0 0 0 0 0 0 0 C x 0 x
0 0 0 0 0 0 0 C 1 0 x
0 0 0 0 0 0 1 C 1 0 23
0 0 0 0 0 0 0 C 1 0 0
0 0 0 0 0 0 0 C 1 0 0
0 0 0 0 0 0 0 C 1 0 0
0 0 0 0 0 0 0 C 1 0 0
0 0 0 0 0 0 0 C 1 0 0
0 0 0 0 0 0 0 C 1 0 0
0 0 0 0 0 0 0 C 1 0 0
0 0 0 0 0 0 0 C 1 0 0
0 0 0 0 0 0 0 C 1 0 0
0 0 0 0 0 0 0 C 1 0 0
0 0 0 0 0 0 0 C 1 0 0
0 0 0 0 0 0 0 C 1 0 0
0 0 0 0 0 0 0 C 1 0 0
0 0 0 0 0 0 0 C 1 0 0
0 0 0 0 0 0 0 C 1 0 0
repeat(2) 0 0 0 0 0 0 0 C 1 1 x
*/

/* Test case 02_P02T01:
M N progIn reset progLoad start result clk valid done output
0 0 0 0 0 0 0 0 x x x
0 0 0 0 0 0 0 1 x x x
0 0 0 1 0 0 0 0 x x x
0 0 0 1 0 0 0 1 0 0 x
0 0 0 0 0 0 0 0 0 x x
0 0 0 0 0 0 0 1 0 x x
0 0 0 0 0 0 0 0 0 x x
0 0 0 0 0 0 0 1 0 x x
0 0 0 0 0 0 0 0 0 x x
0 0 0 0 0 0 0 1 0 x x
0 0 0 0 0 0 0 0 0 x x
0 0 0 0 0 0 0 1 0 x x
0 0 0 0 0 0 0 0 0 x x
0 0 0 0 0 0 0 1 0 x x
0 0 0 0 0 0 0 0 0 x x
0 0 0 0 0 0 0 1 0 x x
0 0 0 0 0 0 0 0 0 x x
0 0 0 0 0 0 0 1 0 x x
0 0 0 0 0 0 0 0 0 x x
0 0 0 0 0 0 0 1 0 x x
0 0 0 0 0 0 0 0 0 x x
0 0 0 0 0 0 0 1 0 x x
0 0 0 0 0 0 0 0 0 x x
0 0 0 0 0 0 0 1 0 x x
0 0 0 0 0 0 0 0 0 x x
0 0 0 0 0 0 0 1 0 x x
0 0 0 0 0 0 0 0 0 x x
0 0 0 0 0 0 0 1 0 x x
0 0 0 0 0 0 0 0 0 x x
0 0 0 0 0 0 0 1 0 x x
0 0 0 0 0 0 0 0 0 x x
0 0 0 0 0 0 0 1 0 x x
0 0 0 0 0 0 0 0 0 x x
0 0 0 0 0 0 0 1 0 x x
0 0 0 0 0 0 0 0 0 x x
0 0 0 0 0 0 0 1 0 x x
0 0 0 0 0 0 0 0 0 x x
0 0 0 0 0 0 0 1 0 x x
0 0 0 0 0 0 0 0 0 x x
0 0 0 0 0 0 0 1 0 x x
0 0 0 0 0 0 0 0 0 x x
0 0 0 0 0 0 0 1 0 x x
0 0 0 0 0 0 0 0 0 x x
0 0 0 0 0 0 0 1 0 x x
0 0 257 0 1 0 0 0 0 x x
0 0 257 0 1 0 0 1 0 x x
0 0 12291 0 1 0 0 0 0 x x
0 0 12291 0 1 0 0 1 0 x x
0 0 355 0 1 0 0 0 0 x x
0 0 355 0 1 0 0 1 0 x x
0 0 4352 0 1 0 0 0 0 x x
0 0 4352 0 1 0 0 1 0 x x
0 0 258 0 1 0 0 0 0 x x
0 0 258 0 1 0 0 1 0 x x
0 0 12295 0 1 0 0 0 0 x x
0 0 12295 0 1 0 0 1 0 x x
0 0 16128 0 1 0 0 0 0 x x
0 0 16128 0 1 0 0 1 0 x x
0 0 4353 0 1 0 0 0 0 x x
0 0 4353 0 1 0 0 1 0 x x
0 0 16128 0 1 0 0 0 0 x x
0 0 16128 0 1 0 0 1 0 x x
0 0 0 0 0 1 0 0 x x x
0 0 0 0 0 1 0 1 x 0 x
0 0 0 0 0 0 0 0 x 0 x
0 0 0 0 0 0 0 1 x 0 x
0 0 0 0 0 0 0 0 x 0 x
0 0 0 0 0 0 0 1 x 0 x
0 0 0 0 0 0 0 0 x 0 x
0 0 0 0 0 0 0 1 x 0 x
0 0 0 0 0 0 0 0 x 0 x
0 0 0 0 0 0 0 1 x 0 x
0 0 0 0 0 0 0 0 x 0 x
0 0 0 0 0 0 0 1 x 0 x
0 0 0 0 0 0 0 0 x 0 x
0 0 0 0 0 0 0 1 x 0 x
0 0 0 0 0 0 0 0 x 0 x
0 0 0 0 0 0 0 1 x 0 x
0 0 0 0 0 0 0 0 x 0 x
0 0 0 0 0 0 0 1 x 0 x
0 0 0 0 0 0 0 0 x 0 x
0 0 0 0 0 0 0 1 x 0 x
0 0 0 0 0 0 0 0 x 0 x
0 0 0 0 0 0 0 1 x 0 x
0 0 0 0 0 0 0 0 x 0 x
0 0 0 0 0 0 0 1 x 0 x
0 0 0 0 0 0 0 0 x 0 x
0 0 0 0 0 0 0 1 x 0 x
0 0 0 0 0 0 0 0 x 0 x
0 0 0 0 0 0 0 1 x 0 x
0 0 0 0 0 0 0 0 x 0 x
0 0 0 0 0 0 0 1 x 0 x
0 0 0 0 0 0 0 0 x 0 x
0 0 0 0 0 0 0 1 x 0 x
0 0 0 0 0 0 0 0 x 0 x
0 0 0 0 0 0 0 1 x 0 x
0 0 0 0 0 0 0 0 x 0 x
0 0 0 0 0 0 0 1 x 0 x
0 0 0 0 0 0 0 0 x 0 x
0 0 0 0 0 0 0 1 x 0 x
0 0 0 0 0 0 0 0 x 0 x
0 0 0 0 0 0 0 1 x 0 x
0 0 0 0 0 0 0 0 x 0 x
0 0 0 0 0 0 0 1 x 0 x
0 0 0 0 0 0 0 0 x 0 x
0 0 0 0 0 0 0 1 x 0 x
0 0 0 0 0 0 0 0 x 0 x
0 0 0 0 0 0 0 1 x 0 x
0 0 0 0 0 0 0 0 x 0 x
0 0 0 0 0 0 0 1 x 0 x
0 0 0 0 0 0 0 0 x 0 x
0 0 0 0 0 0 0 1 x 0 x
0 0 0 0 0 0 0 0 x 0 x
0 0 0 0 0 0 0 1 x 0 x
0 0 0 0 0 0 0 0 x 0 x
0 0 0 0 0 0 0 1 x 0 x
0 0 0 0 0 0 0 0 x 0 x
0 0 0 0 0 0 0 1 x 0 x
0 0 0 0 0 0 0 0 x 0 x
0 0 0 0 0 0 0 1 x 0 x
0 0 0 0 0 0 0 0 x 0 x
0 0 0 0 0 0 0 1 x 0 x
0 0 0 0 0 0 0 0 x 0 x
0 0 0 0 0 0 0 1 x 0 x
0 0 0 0 0 0 0 0 x 0 x
0 0 0 0 0 0 0 1 x 0 x
0 0 0 0 0 0 0 0 x 0 x
0 0 0 0 0 0 0 1 1 0 x
0 0 0 0 0 0 1 0 1 x x
0 0 0 0 0 0 1 1 1 0 1
0 0 0 0 0 0 0 0 1 0 1
0 0 0 0 0 0 0 1 1 0 2
0 0 0 0 0 0 0 0 1 0 2
0 0 0 0 0 0 0 1 1 0 0
0 0 0 0 0 0 0 0 1 0 0
0 0 0 0 0 0 0 1 1 0 0
0 0 0 0 0 0 0 0 1 0 0
0 0 0 0 0 0 0 1 1 0 0
0 0 0 0 0 0 0 0 1 0 0
0 0 0 0 0 0 0 1 1 0 0
0 0 0 0 0 0 0 0 1 0 0
0 0 0 0 0 0 0 1 1 0 0
0 0 0 0 0 0 0 0 1 0 0
0 0 0 0 0 0 0 1 1 0 0
0 0 0 0 0 0 0 0 1 0 0
0 0 0 0 0 0 0 1 1 0 0
0 0 0 0 0 0 0 0 1 0 0
0 0 0 0 0 0 0 1 1 0 0
0 0 0 0 0 0 0 0 1 0 0
0 0 0 0 0 0 0 1 1 0 0
0 0 0 0 0 0 0 0 1 0 0
0 0 0 0 0 0 0 1 1 0 0
0 0 0 0 0 0 0 0 1 0 0
0 0 0 0 0 0 0 1 1 0 0
0 0 0 0 0 0 0 0 1 0 0
0 0 0 0 0 0 0 1 1 0 0
0 0 0 0 0 0 0 0 1 0 0
0 0 0 0 0 0 0 1 1 0 0
0 0 0 0 0 0 0 0 1 0 0
0 0 0 0 0 0 0 1 1 0 0
0 0 0 0 0 0 0 0 1 x 0
0 0 0 0 0 0 0 1 1 1 x
0 0 0 0 0 0 0 0 1 1 x
0 0 0 0 0 0 0 1 1 1 x
*/

/* Test case 21_P08T02:
M N progIn reset progLoad start result clk valid done output
0 0 0 0 0 0 0 C x x x
0 0 0 1 0 0 0 C 0 0 x
repeat(20) 0 0 0 0 0 0 0 C 0 x x
0 0 456 0 1 0 0 C 0 x x
0 0 519 0 1 0 0 C 0 x x
0 0 9216 0 1 0 0 C 0 x x
0 0 4352 0 1 0 0 C 0 x x
0 0 456 0 1 0 0 C 0 x x
0 0 9472 0 1 0 0 C 0 x x
0 0 4353 0 1 0 0 C 0 x x
0 0 384 0 1 0 0 C 0 x x
0 0 515 0 1 0 0 C 0 x x
0 0 9216 0 1 0 0 C 0 x x
0 0 4354 0 1 0 0 C 0 x x
0 0 511 0 1 0 0 C 0 x x
0 0 767 0 1 0 0 C 0 x x
0 0 9472 0 1 0 0 C 0 x x
0 0 4355 0 1 0 0 C 0 x x
0 0 261 0 1 0 0 C 0 x x
0 0 521 0 1 0 0 C 0 x x
0 0 9216 0 1 0 0 C 0 x x
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*/

/* Test case S03_recursion32:
M N progIn reset progLoad start result clk valid done output
0 0 0 0 0 0 0 C x x x
0 0 0 1 0 0 0 C 0 0 x
repeat(20) 0 0 0 0 0 0 0 C 0 x x
0 0 288 0 1 0 0 C 0 x x
0 0 1792 0 1 0 0 C 0 x x
0 0 256 0 1 0 0 C 0 x x
0 0 7176 0 1 0 0 C 0 x x
0 0 4352 0 1 0 0 C 0 x x
0 0 2560 0 1 0 0 C 0 x x
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*/

/* Test case 15_P02T02:
M N progIn reset progLoad start result clk valid done output
0 0 0 0 0 0 0 C x x x
0 0 0 1 0 0 0 C 0 0 x
repeat(20) 0 0 0 0 0 0 0 C 0 x x
0 0 496 0 1 0 0 C 0 x x
0 0 517 0 1 0 0 C 0 x x
0 0 14336 0 1 0 0 C 0 x x
0 0 13061 0 1 0 0 C 0 x x
0 0 256 0 1 0 0 C 0 x x
0 0 4352 0 1 0 0 C 0 x x
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*/

/* Test case 09_P09T01:
M N progIn reset progLoad start result clk valid done output
0 0 0 0 0 0 0 0 x x x
0 0 0 0 0 0 0 1 x x x
0 0 0 1 0 0 0 0 x x x
0 0 0 1 0 0 0 1 0 0 x
0 0 0 0 0 0 0 0 0 x x
0 0 0 0 0 0 0 1 0 x x
0 0 0 0 0 0 0 0 0 x x
0 0 0 0 0 0 0 1 0 x x
0 0 0 0 0 0 0 0 0 x x
0 0 0 0 0 0 0 1 0 x x
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*/

/* Test case S04_SSUM:
M N progIn reset progLoad start result clk valid done output
0 0 0 0 0 0 0 C x x x
0 0 0 1 0 0 0 C 0 0 x
repeat(20) 0 0 0 0 0 0 0 C 0 x x
0 0 15872 0 1 0 0 C 0 x x
0 0 4108 0 1 0 0 C 0 x x
0 0 4352 0 1 0 0 C 0 x x
0 0 4109 0 1 0 0 C 0 x x
0 0 4353 0 1 0 0 C 0 x x
0 0 384 0 1 0 0 C 0 x x
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*/

/* Test case 03_P03T01:
M N progIn reset progLoad start result clk valid done output
0 0 0 0 0 0 0 0 x x x
0 0 0 0 0 0 0 1 x x x
0 0 0 1 0 0 0 0 x x x
0 0 0 1 0 0 0 1 0 0 x
0 0 0 0 0 0 0 0 0 x x
0 0 0 0 0 0 0 1 0 x x
0 0 0 0 0 0 0 0 0 x x
0 0 0 0 0 0 0 1 0 x x
0 0 0 0 0 0 0 0 0 x x
0 0 0 0 0 0 0 1 0 x x
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*/

/* Test case 22_P09T02:
M N progIn reset progLoad start result clk valid done output
0 0 0 0 0 0 0 C x x x
0 0 0 1 0 0 0 C 0 0 x
repeat(20) 0 0 0 0 0 0 0 C 0 x x
0 0 435 0 1 0 0 C 0 x x
0 0 515 0 1 0 0 C 0 x x
0 0 11264 0 1 0 0 C 0 x x
0 0 4352 0 1 0 0 C 0 x x
0 0 435 0 1 0 0 C 0 x x
0 0 515 0 1 0 0 C 0 x x
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*/

/* Test case S05_SSUM_in_sub:
M N progIn reset progLoad start result clk valid done output
0 0 0 0 0 0 0 C x x x
0 0 0 1 0 0 0 C 0 0 x
repeat(20) 0 0 0 0 0 0 0 C 0 x x
0 0 257 0 1 0 0 C 0 x x
0 0 6144 0 1 0 0 C 0 x x
0 0 258 0 1 0 0 C 0 x x
0 0 7178 0 1 0 0 C 0 x x
0 0 4352 0 1 0 0 C 0 x x
0 0 6400 0 1 0 0 C 0 x x
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*/

/* Test case 16_P03T02:
M N progIn reset progLoad start result clk valid done output
0 0 0 0 0 0 0 C x x x
0 0 0 1 0 0 0 C 0 0 x
repeat(20) 0 0 0 0 0 0 0 C 0 x x
0 0 4628 0 1 0 0 C 0 x x
0 0 4352 0 1 0 0 C 0 x x
0 0 4629 0 1 0 0 C 0 x x
0 0 4353 0 1 0 0 C 0 x x
0 0 4630 0 1 0 0 C 0 x x
0 0 4354 0 1 0 0 C 0 x x
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*/

/* Test case 10_P10T01:
M N progIn reset progLoad start result clk valid done output
0 0 0 0 0 0 0 0 x x x
0 0 0 0 0 0 0 1 x x x
0 0 0 1 0 0 0 0 x x x
0 0 0 1 0 0 0 1 0 0 x
0 0 0 0 0 0 0 0 0 x x
0 0 0 0 0 0 0 1 0 x x
0 0 0 0 0 0 0 0 0 x x
0 0 0 0 0 0 0 1 0 x x
0 0 0 0 0 0 0 0 0 x x
0 0 0 0 0 0 0 1 0 x x
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*/

/* Test case 04_P04T01:
M N progIn reset progLoad start result clk valid done output
0 0 0 0 0 0 0 0 x x x
0 0 0 0 0 0 0 1 x x x
0 0 0 1 0 0 0 0 x x x
0 0 0 1 0 0 0 1 0 0 x
0 0 0 0 0 0 0 0 0 x x
0 0 0 0 0 0 0 1 0 x x
0 0 0 0 0 0 0 0 0 x x
0 0 0 0 0 0 0 1 0 x x
0 0 0 0 0 0 0 0 0 x x
0 0 0 0 0 0 0 1 0 x x
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*/

/* Test case 23_P10T02:
M N progIn reset progLoad start result clk valid done output
0 0 0 0 0 0 0 C x x x
0 0 0 1 0 0 0 C 0 0 x
repeat(20) 0 0 0 0 0 0 0 C 0 x x
0 0 264 0 1 0 0 C 0 x x
0 0 1792 0 1 0 0 C 0 x x
0 0 273 0 1 0 0 C 0 x x
0 0 6144 0 1 0 0 C 0 x x
0 0 529 0 1 0 0 C 0 x x
0 0 8192 0 1 0 0 C 0 x x
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*/

/* Test case 17_P04T02:
M N progIn reset progLoad start result clk valid done output
0 0 0 0 0 0 0 C x x x
0 0 0 1 0 0 0 C 0 0 x
repeat(20) 0 0 0 0 0 0 0 C 0 x x
0 0 256 0 1 0 0 C 0 x x
0 0 14592 0 1 0 0 C 0 x x
0 0 256 0 1 0 0 C 0 x x
0 0 12549 0 1 0 0 C 0 x x
0 0 12294 0 1 0 0 C 0 x x
0 0 257 0 1 0 0 C 0 x x
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*/

/* Test case 11_P11T01:
M N progIn reset progLoad start result clk valid done output
0 0 0 0 0 0 0 0 x x x
0 0 0 0 0 0 0 1 x x x
0 0 0 1 0 0 0 0 x x x
0 0 0 1 0 0 0 1 0 0 x
0 0 0 0 0 0 0 0 0 x x
0 0 0 0 0 0 0 1 0 x x
0 0 0 0 0 0 0 0 0 x x
0 0 0 0 0 0 0 1 0 x x
0 0 0 0 0 0 0 0 0 x x
0 0 0 0 0 0 0 1 0 x x
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*/

/* Test case 05_P05T01:
M N progIn reset progLoad start result clk valid done output
0 0 0 0 0 0 0 0 x x x
0 0 0 0 0 0 0 1 x x x
0 0 0 1 0 0 0 0 x x x
0 0 0 1 0 0 0 1 0 0 x
0 0 0 0 0 0 0 0 0 x x
0 0 0 0 0 0 0 1 0 x x
0 0 0 0 0 0 0 0 0 x x
0 0 0 0 0 0 0 1 0 x x
0 0 0 0 0 0 0 0 0 x x
0 0 0 0 0 0 0 1 0 x x
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*/

/* Test case 24_P11T02:
M N progIn reset progLoad start result clk valid done output
0 0 0 0 0 0 0 C x x x
0 0 0 1 0 0 0 C 0 0 x
repeat(20) 0 0 0 0 0 0 0 C 0 x x
0 0 256 0 1 0 0 C 0 x x
0 0 1536 0 1 0 0 C 0 x x
0 0 259 0 1 0 0 C 0 x x
0 0 1792 0 1 0 0 C 0 x x
0 0 2304 0 1 0 0 C 0 x x
0 0 6144 0 1 0 0 C 0 x x
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*/

/* Test case 18_P05T02:
M N progIn reset progLoad start result clk valid done output
0 0 0 0 0 0 0 C x x x
0 0 0 1 0 0 0 C 0 0 x
repeat(20) 0 0 0 0 0 0 0 C 0 x x
0 0 260 0 1 0 0 C 0 x x
0 0 516 0 1 0 0 C 0 x x
0 0 14336 0 1 0 0 C 0 x x
0 0 14592 0 1 0 0 C 0 x x
0 0 12569 0 1 0 0 C 0 x x
0 0 257 0 1 0 0 C 0 x x
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*/

/* Test case 12_P12T01:
M N progIn reset progLoad start result clk valid done output
0 0 0 0 0 0 0 0 x x x
0 0 0 0 0 0 0 1 x x x
0 0 0 1 0 0 0 0 x x x
0 0 0 1 0 0 0 1 0 0 x
0 0 0 0 0 0 0 0 0 x x
0 0 0 0 0 0 0 1 0 x x
0 0 0 0 0 0 0 0 0 x x
0 0 0 0 0 0 0 1 0 x x
0 0 0 0 0 0 0 0 0 x x
0 0 0 0 0 0 0 1 0 x x
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*/

/* Test case 06_P06T01:
M N progIn reset progLoad start result clk valid done output
0 0 0 0 0 0 0 0 x x x
0 0 0 0 0 0 0 1 x x x
0 0 0 1 0 0 0 0 x x x
0 0 0 1 0 0 0 1 0 0 x
0 0 0 0 0 0 0 0 0 x x
0 0 0 0 0 0 0 1 0 x x
0 0 0 0 0 0 0 0 0 x x
0 0 0 0 0 0 0 1 0 x x
0 0 0 0 0 0 0 0 0 x x
0 0 0 0 0 0 0 1 0 x x
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*/

/* Test case 25_P12T02:
M N progIn reset progLoad start result clk valid done output
0 0 0 0 0 0 0 C x x x
0 0 0 1 0 0 0 C 0 0 x
repeat(20) 0 0 0 0 0 0 0 C 0 x x
0 0 511 0 1 0 0 C 0 x x
0 0 513 0 1 0 0 C 0 x x
0 0 15360 0 1 0 0 C 0 x x
0 0 4352 0 1 0 0 C 0 x x
0 0 257 0 1 0 0 C 0 x x
0 0 767 0 1 0 0 C 0 x x
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*/

/* Test case 19_P06T02:
M N progIn reset progLoad start result clk valid done output
0 0 0 0 0 0 0 C x x x
0 0 0 1 0 0 0 C 0 0 x
repeat(20) 0 0 0 0 0 0 0 C 0 x x
0 0 3072 0 1 0 0 C 0 x x
0 0 3328 0 1 0 0 C 0 x x
0 0 2048 0 1 0 0 C 0 x x
0 0 4352 0 1 0 0 C 0 x x
0 0 2304 0 1 0 0 C 0 x x
0 0 4353 0 1 0 0 C 0 x x
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*/

/* Test case 13_P13T01:
M N progIn reset progLoad start result clk valid done output
0 0 0 0 0 0 0 0 x x x
0 0 0 0 0 0 0 1 x x x
0 0 0 1 0 0 0 0 x x x
0 0 0 1 0 0 0 1 0 0 x
0 0 0 0 0 0 0 0 0 x x
0 0 0 0 0 0 0 1 0 x x
0 0 0 0 0 0 0 0 0 x x
0 0 0 0 0 0 0 1 0 x x
0 0 0 0 0 0 0 0 0 x x
0 0 0 0 0 0 0 1 0 x x
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*/

/* Test case 07_P07T01:
M N progIn reset progLoad start result clk valid done output
0 0 0 0 0 0 0 0 x x x
0 0 0 0 0 0 0 1 x x x
0 0 0 1 0 0 0 0 x x x
0 0 0 1 0 0 0 1 0 0 x
0 0 0 0 0 0 0 0 0 x x
0 0 0 0 0 0 0 1 0 x x
0 0 0 0 0 0 0 0 0 x x
0 0 0 0 0 0 0 1 0 x x
0 0 0 0 0 0 0 0 0 x x
0 0 0 0 0 0 0 1 0 x x
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*/

/* Test case 26_P13T02:
M N progIn reset progLoad start result clk valid done output
0 0 0 0 0 0 0 C x x x
0 0 0 1 0 0 0 C 0 0 x
repeat(20) 0 0 0 0 0 0 0 C 0 x x
0 0 280 0 1 0 0 C 0 x x
0 0 15616 0 1 0 0 C 0 x x
0 0 4106 0 1 0 0 C 0 x x
0 0 4352 0 1 0 0 C 0 x x
0 0 4107 0 1 0 0 C 0 x x
0 0 4353 0 1 0 0 C 0 x x
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*/
