// Digital circuit ALU_Me.dig as structural Verilog
module ALU_Me (
  input  [7:0] accA,
  input  [7:0] accB,
  input  [5:0] Opcode,
  output [7:0] ACCA_2
);

  wire [7:0] A_B, A_B_t, A_B_t_t, A_B_t_t_t, A_gt__gt__gt_B, A_gt__gt_B, A_lt__lt__lt_B, A_lt__lt_B,
       A_plus_B, AandB, AorB, Arithmetric, AxorB, Division, Logic, notA, Shift;

  Add #(.Bits(8)) add_1 (.a(accA), .b(accB), .c_i(1'b0), .s(A_plus_B));  // open: c_o
  Sub #(.Bits(8)) sub_1 (.a(accA), .b(accB), .c_i(1'b0), .s(A_B_t_t));  // open: c_o
  Mul #(.Bits(4)) mul_1 (.a(accA[3:0]), .b(accB[3:0]), .mul(A_B_t));
  Multiplexer #(.Selector_Bits(2), .Bits(8)) multiplexer_1 (
    .sel(Opcode[1:0]), .in_0(A_plus_B), .in_1(A_B_t_t), .in_2(A_B_t), .in_3({8{1'b0}}), .out(Arithmetric));
  Multiplexer #(.Selector_Bits(2), .Bits(8)) multiplexer_2 (
    .sel(Opcode[3:2]), .in_0(Arithmetric), .in_1(Division), .in_2(Logic), .in_3(Shift), .out(ACCA_2));
  Div #(.Bits(8)) div_1 (.a(accA), .b(accB), .q(A_B_t_t_t), .r(A_B));
  Multiplexer #(.Selector_Bits(2), .Bits(8)) multiplexer_3 (
    .sel(Opcode[1:0]), .in_0(A_B_t_t_t), .in_1(A_B), .in_2({8{1'b0}}), .in_3({8{1'b0}}), .out(Division));
  assign AandB = accA & accB;  // And and_1, 8 bits wide
  assign AorB = accA | accB;  // Or or_1, 8 bits wide
  assign AxorB = accA ^ accB;  // XOr xor_1, 8 bits wide
  assign notA = ~accA;  // Not not_1, 8 bits wide
  BarrelShifter #(.Bits(8)) barrelshifter_1 (.in(accA), .shift(accB[3:0]), .out(A_lt__lt_B));
  BarrelShifter #(.Bits(8), .direction("right")) barrelshifter_2 (.in(accA), .shift(accB[3:0]), .out(A_gt__gt_B));
  BarrelShifter #(.Bits(8), .barrelShifterMode("rotate")) barrelshifter_3 (
    .in(accA), .shift(accB[3:0]), .out(A_lt__lt__lt_B));
  BarrelShifter #(.Bits(8), .barrelShifterMode("rotate"), .direction("right")) barrelshifter_4 (
    .in(accA), .shift(accB[3:0]), .out(A_gt__gt__gt_B));
  Multiplexer #(.Selector_Bits(2), .Bits(8)) multiplexer_4 (
    .sel(Opcode[1:0]), .in_0(AandB), .in_1(AorB), .in_2(AxorB), .in_3(notA), .out(Logic));
  Multiplexer #(.Selector_Bits(2), .Bits(8)) multiplexer_5 (
    .sel(Opcode[1:0]), .in_0(A_lt__lt_B), .in_1(A_gt__gt_B), .in_2(A_lt__lt__lt_B), .in_3(A_gt__gt__gt_B),
    .out(Shift));

  // Other names for the same wires on the sheet: A[7:0] = accA; B[7:0] = accB; CMD[1:0] = Opcode[1:0];
  //   Type[1:0] = Opcode[3:2]; Group[1:0] = Opcode[5:4]

  // Notes on the sheet:
  //   Arithmetric
  //   Division
  //   Logic
  //   Shift
endmodule
